// Logisim project CPU_PROT_1.circ as structural Verilog: 1 circuit, main circuit main
module main (
);

  wire button_1_out, button_2_out;
  wire [3:0] A_q, adder_1_out, register_1_q;

  Register #(.width(4)) register_1 (.Q(register_1_q), .clr(button_1_out));  // open: D, en, clk
  Register #(.width(4)) A (.Q(A_q), .clr(button_2_out));  // open: D, en, clk
  Button button_1 (.out(button_1_out));
  Button button_2 (.out(button_2_out));
  Adder #(.width(4)) adder_1 (.a(register_1_q), .b(A_q), .out(adder_1_out));  // open: cin, cout
  Register #(.width(4)) register_2 (.D(adder_1_out));  // open: en, clk, Q, clr
endmodule
