// Logisim project LOGSIM_BASIC_1.circ as structural Verilog: 3 circuits, main circuit principe
module principe (
  input  A,
  input  B,
  input  C,
  output S
);

  wire and_1_out, and_2_out;

  and and_1 (and_1_out, ~A, ~C);  // AND_Gate
  and and_2 (and_2_out, B, C);
  or or_1 (S, and_1_out, and_2_out);

  // Notes on the sheet:
  //   S = (A'.C') + (B.C)
endmodule

module using (
  input  in_1,
  input  in_2,
  input  in_3,
  input  in_4,
  output out_5,
  output out_6
);

  xor xor_1 (out_6, in_3, in_4);
endmodule

module MY_XOR (
  input  A,
  input  B,
  output out_3
);

  wire and1_out, and2_out;

  and and1 (and1_out, A, ~B);  // AND_Gate
  and and2 (and2_out, ~B, A);  // AND_Gate
  or or1 (out_3, and1_out, and2_out);

  // Notes on the sheet:
  //   XOR
  //   A ⊕ B = AB' + A'B
  //   AB'
  //   A'B
  //   AB'+A'B
endmodule
