// Logisim project displays_visuais.circ as structural Verilog: 2 circuits, main circuit main
module main (
  input  [6:0] in_1
);

  Hex_Digit_Display hex_digit_display_1 (.value({1'b0, in_1[6:4]}));  // open: dp
  Hex_Digit_Display hex_digit_display_2 (.value(in_1[3:0]));  // open: dp

  // Notes on the sheet:
  //   ? x 16
  //   ? x 1
  //   +
endmodule

module VisorDecimal_Puro (
  input  [3:0] in_1
);

  wire buffer_1_out, buffer_2_out, buffer_3_out, buffer_4_out, buffer_5_out, buffer_6_out, not_1_out,
       not_2_out, not_3_out;

  not not_1 (not_1_out, 1'b0);
  buf buffer_1 (buffer_1_out, not_1_out);
  buf buffer_2 (buffer_2_out, not_1_out);
  buf buffer_3 (buffer_3_out, not_1_out);
  not not_2 (not_2_out, not_1_out);
  buf buffer_4 (buffer_4_out, not_1_out);
  buf buffer_5 (buffer_5_out, not_1_out);
  buf buffer_6 (buffer_6_out, not_1_out);
  not not_3 (not_3_out, not_1_out);
  _7_Segment_Display u_7_segment_display_1 (
    .g(not_2_out), .f(buffer_3_out), .a(buffer_2_out), .b(buffer_1_out), .e(buffer_4_out), .d(buffer_5_out),
    .c(buffer_6_out), .dp(not_3_out));
endmodule
