// Logisim project processador-meu.circ as structural Verilog: 8 circuits, main circuit main
module main (
  input  [3:0] in_1,
  input  [3:0] in_2,
  input  [3:0] in_3,
  input  [3:0] in_4,
  input  [7:0] in_5,
  input  [7:0] in_6,
  input  [3:0] in_7,
  input  [3:0] in_8,
  input  [2:0] in_9,
  output [4:0] out_10,
  output [4:0] out_11,
  output [8:0] Saida_0_125,
  output [3:0] out_13
);

  wire clock_1_out, clock_2_out;

  Hex_Digit_Display hex_digit_display_1 (.value(in_1));  // open: dp
  Hex_Digit_Display hex_digit_display_2 (.value(in_3));  // open: dp
  Hex_Digit_Display hex_digit_display_3 (.value(in_5[7:4]));  // open: dp
  Clock clock_1 (.out(clock_1_out));
  Hex_Digit_Display hex_digit_display_4 (.value(in_5[3:0]));  // open: dp
  ula_4b ula_4b_1 (.B(in_7), .A(in_8), .Op(in_9), .R(out_13));
  s4b s4b_1 (.clockIn(clock_1_out), .in1(in_1), .in2(in_3), .out1(out_10));
  Hex_Digit_Display hex_digit_display_5 (.value({3'b000, Saida_0_125[8]}));  // open: dp
  Adder adder_1 (.a(in_5), .b(in_6), .out(Saida_0_125[7:0]), .cout(Saida_0_125[8]));  // open: cin
  Hex_Digit_Display hex_digit_display_6 (.value({3'b000, out_10[4]}));  // open: dp
  Hex_Digit_Display hex_digit_display_7 (.value(Saida_0_125[7:4]));  // open: dp
  Hex_Digit_Display hex_digit_display_8 (.value(out_10[3:0]));  // open: dp
  Hex_Digit_Display hex_digit_display_9 (.value(Saida_0_125[3:0]));  // open: dp
  Hex_Digit_Display hex_digit_display_10 (.value(in_2));  // open: dp
  Hex_Digit_Display hex_digit_display_11 (.value(in_4));  // open: dp
  Clock clock_2 (.out(clock_2_out));
  s4b_2 s4b_2_1 (.in1(in_2), .in2(in_4), .clockIn(clock_2_out), .out1(out_11));
  Hex_Digit_Display hex_digit_display_12 (.value({3'b000, out_11[4]}));  // open: dp
  Hex_Digit_Display hex_digit_display_13 (.value(out_11[3:0]));  // open: dp

  // Notes on the sheet:
  //   Entrada 0-15
  //   Entrada 0-63
  //   16
  //   128 64 32 16 8 4 2 1
  //   1
  //   256
  //   op0 - 0 = Aritimetica | 1 = Logica
  //   op1 - 0 = Soma | 1 = Subtração
  //   op2 - 0 = And | 1 = Or
  //   000 = Soma
  //   010 = Subtração
  //   001 = And
  //   101 = Or
  //   Saida 1-30
  //   16
  //   Entrada 0-15
  //   1
  //   Saida 1-30
endmodule

module s4b (
  input  clockIn,
  input  [3:0] in1,
  input  [3:0] in2,
  output [4:0] out1
);

  wire adder_1_cout, adder_1_out, adder_2_cout, adder_2_out, adder_3_cout, adder_3_out, adder_4_cout,
       adder_4_out;

  Adder #(.width(1)) adder_1 (.a(in1[0]), .b(in2[0]), .out(adder_1_out), .cin(1'b0), .cout(adder_1_cout));
  Adder #(.width(1)) adder_2 (.a(in1[1]), .b(in2[1]), .out(adder_2_out), .cin(adder_1_cout), .cout(adder_2_cout));
  Adder #(.width(1)) adder_3 (.a(in1[2]), .b(in2[2]), .out(adder_3_out), .cin(adder_2_cout), .cout(adder_3_cout));
  Adder #(.width(1)) adder_4 (.a(in1[3]), .b(in2[3]), .out(adder_4_out), .cin(adder_3_cout), .cout(adder_4_cout));
  D_Flip_Flop d_ff_1 (.clk(clockIn), .D(adder_1_out), .Q(out1[0]));  // open: Qn, preset, reset
  D_Flip_Flop d_ff_2 (.clk(clockIn), .D(adder_2_out), .Q(out1[1]));  // open: Qn, preset, reset
  D_Flip_Flop d_ff_3 (.clk(clockIn), .D(adder_3_out), .Q(out1[2]));  // open: Qn, preset, reset
  D_Flip_Flop d_ff_4 (.clk(clockIn), .D(adder_4_out), .Q(out1[3]));  // open: Qn, preset, reset
  D_Flip_Flop d_ff_5 (.clk(clockIn), .D(adder_4_cout), .Q(out1[4]));  // open: Qn, preset, reset
  s4b_2 s4b_2_1 ();  // open: in1, in2, clockIn, out1
endmodule

module s1b (
  input  carryIn,
  input  in1,
  input  in2,
  output out1,
  output carryOut
);

  wire and_2_out, not_1_out, or_1_out, or_2_out;

  or or_1 (or_1_out, in2, in1, carryIn);
  and and_1 (carryOut, or_1_out, or_2_out);
  and and_2 (and_2_out, carryIn, in1, in2);
  ExactlyOne xor_1 (.out(out1), .in0(carryIn), .in1(in1), .in2(in2));
  not not_1 (not_1_out, out1);
  or or_2 (or_2_out, and_2_out, not_1_out);
endmodule

module s1b_2 (
  input  A,
  input  B,
  input  CI,
  output CO,
  output R
);

  wire and_1_out, and_2_out, xor_1_out;

  xor xor_1 (xor_1_out, A, B);
  and and_1 (and_1_out, A, B);
  xor xor_2 (R, CI, xor_1_out);
  and and_2 (and_2_out, xor_1_out, CI);
  or or_1 (CO, and_2_out, and_1_out);
endmodule

module s4b_2 (
  input  clockIn,
  input  [3:0] in1,
  input  [3:0] in2,
  output [4:0] out1
);

  wire s1b_2_1_co, s1b_2_1_r, s1b_2_2_co, s1b_2_2_r, s1b_2_3_co, s1b_2_3_r, s1b_2_4_co, s1b_2_4_r;

  s1b_2 s1b_2_1 (.CI(1'b0), .A(in1[0]), .B(in2[0]), .CO(s1b_2_1_co), .R(s1b_2_1_r));
  s1b_2 s1b_2_2 (.CI(s1b_2_1_co), .A(in1[1]), .B(in2[1]), .CO(s1b_2_2_co), .R(s1b_2_2_r));
  s1b_2 s1b_2_3 (.CI(s1b_2_2_co), .A(in1[2]), .B(in2[2]), .CO(s1b_2_3_co), .R(s1b_2_3_r));
  s1b_2 s1b_2_4 (.CI(s1b_2_3_co), .A(in1[3]), .B(in2[3]), .CO(s1b_2_4_co), .R(s1b_2_4_r));
  D_Flip_Flop d_ff_1 (.clk(clockIn), .D(s1b_2_1_r), .Q(out1[0]));  // open: Qn, preset, reset
  D_Flip_Flop d_ff_2 (.clk(clockIn), .D(s1b_2_2_r), .Q(out1[1]));  // open: Qn, preset, reset
  D_Flip_Flop d_ff_3 (.clk(clockIn), .D(s1b_2_3_r), .Q(out1[2]));  // open: Qn, preset, reset
  D_Flip_Flop d_ff_4 (.clk(clockIn), .D(s1b_2_4_r), .Q(out1[3]));  // open: Qn, preset, reset
  D_Flip_Flop d_ff_5 (.clk(clockIn), .D(s1b_2_4_co), .Q(out1[4]));  // open: Qn, preset, reset
endmodule

module ula_4b_f1 (
  input  [3:0] A,
  input  [3:0] B,
  input  [1:0] Op,
  output [3:0] R
);

  wire [3:0] adder_1_out, and_1_out, or_1_out, xor_1_out;

  assign and_1_out = A & B;  // AND_Gate and_1, 4 bits wide
  assign or_1_out = A | B;  // OR_Gate or_1, 4 bits wide
  xor xor_1 (xor_1_out[0], B[0], Op[0]);
  xor xor_2 (xor_1_out[1], B[1], Op[0]);
  xor xor_3 (xor_1_out[2], B[2], Op[0]);
  xor xor_4 (xor_1_out[3], B[3], Op[0]);
  Adder #(.width(4)) adder_1 (.a(A), .b(xor_1_out), .out(adder_1_out), .cin(Op[1]));  // open: cout
  Multiplexer #(.select(2), .width(4)) multiplexer_1 (
    .in0(adder_1_out), .in1(adder_1_out), .in2(and_1_out), .in3(or_1_out), .out(R));  // open: sel
endmodule

module ula_4b_f2 (
  input  [3:0] A,
  input  [3:0] B,
  input  [1:0] Op,
  output [3:0] R
);

  wire [3:0] adder_1_out, and_1_out, multiplexer_1_out, or_1_out, xor_1_out;

  assign and_1_out = A & B;  // AND_Gate and_1, 4 bits wide
  assign or_1_out = A | B;  // OR_Gate or_1, 4 bits wide
  xor xor_1 (xor_1_out[0], B[0], Op[0]);
  xor xor_2 (xor_1_out[1], B[1], Op[0]);
  xor xor_3 (xor_1_out[2], B[2], Op[0]);
  xor xor_4 (xor_1_out[3], B[3], Op[0]);
  Multiplexer #(.width(4)) multiplexer_1 (.in0(and_1_out), .in1(or_1_out), .out(multiplexer_1_out), .sel(Op[0]));
  Adder #(.width(4)) adder_1 (.a(A), .b(xor_1_out), .out(adder_1_out), .cin(Op[0]));  // open: cout
  Multiplexer #(.width(4)) multiplexer_2 (.in0(adder_1_out), .in1(multiplexer_1_out), .out(R), .sel(Op[1]));
endmodule

module ula_4b (
  input  [3:0] A,
  input  [3:0] B,
  input  [2:0] Op,
  output [3:0] R
);

  wire [3:0] adder_1_out, and_1_out, multiplexer_1_out, multiplexer_2_out, or_1_out, subtractor_1_out;

  Adder #(.width(4)) adder_1 (.a(A), .b(B), .out(adder_1_out));  // open: cin, cout
  Subtractor #(.width(4)) subtractor_1 (.a(A), .b(B), .out(subtractor_1_out));  // open: bin, bout
  assign and_1_out = A & B;  // AND_Gate and_1, 4 bits wide
  assign or_1_out = A | B;  // OR_Gate or_1, 4 bits wide
  Multiplexer #(.width(4)) multiplexer_1 (
    .in0(adder_1_out), .in1(subtractor_1_out), .out(multiplexer_1_out), .sel(Op[1]));
  Multiplexer #(.width(4)) multiplexer_2 (.in0(and_1_out), .in1(or_1_out), .out(multiplexer_2_out), .sel(Op[2]));
  Multiplexer #(.width(4)) multiplexer_3 (.in0(multiplexer_1_out), .in1(multiplexer_2_out), .out(R), .sel(Op[0]));
endmodule
