// Logisim project processador-seguindo-viana.circ as structural Verilog
module adder_1b (
  input  A,
  input  CI,
  input  B,
  output S,
  output CO
);

  wire and_1_out, and_2_out, xor_1_out;

  xor xor_1 (xor_1_out, A, B);
  and and_1 (and_1_out, A, B);
  xor xor_2 (S, CI, xor_1_out);
  and and_2 (and_2_out, xor_1_out, CI);
  or or_1 (CO, and_2_out, and_1_out);

  // Notes on the sheet:
  //   LF - Adder 1b
endmodule

module adder_4b (
  input  [3:0] BusA,
  input  [3:0] BusB,
  output [3:0] _16_8_4_2_1
);

  wire adder_1b_1_co, adder_1b_2_co, adder_1b_3_co, adder_1b_4_co;

  LED A3 (.in(BusA[3]));
  LED B3 (.in(BusB[3]));
  LED cO (.in(adder_1b_1_co));
  LED A0 (.in(BusA[0]));
  LED A1 (.in(BusA[1]));
  LED A2 (.in(BusA[2]));
  LED B0 (.in(BusB[0]));
  LED B1 (.in(BusB[1]));
  LED B2 (.in(BusB[2]));
  LED S0 (.in(_16_8_4_2_1[0]));
  LED S1 (.in(_16_8_4_2_1[1]));
  LED S2 (.in(_16_8_4_2_1[2]));
  LED S3 (.in(_16_8_4_2_1[3]));
  adder_1b adder_1b_1 (.CI(adder_1b_2_co), .A(BusA[3]), .B(BusB[3]), .S(_16_8_4_2_1[3]), .CO(adder_1b_1_co));
  adder_1b adder_1b_2 (.CI(adder_1b_3_co), .A(BusA[2]), .B(BusB[2]), .S(_16_8_4_2_1[2]), .CO(adder_1b_2_co));
  adder_1b adder_1b_3 (.CI(adder_1b_4_co), .A(BusA[1]), .B(BusB[1]), .S(_16_8_4_2_1[1]), .CO(adder_1b_3_co));
  adder_1b adder_1b_4 (.A(BusA[0]), .B(BusB[0]), .S(_16_8_4_2_1[0]), .CO(adder_1b_4_co));  // open: CI

  // Notes on the sheet:
  //   8 4 2 1
  //   8 4 2 1
  //   Este Adder possui carryOut. Ou seja, as entradas são de 4b, a saida de 5b
  //   LF - Adder 4b
endmodule

module ula_4b (
  input  [3:0] A,
  input  [3:0] B,
  input  [2:0] Op
);
endmodule

module buffer_4b (
  input  [3:0] A,
  output [3:0] out_2
);

  buf buffer_1 (out_2[3], A[3]);
  buf buffer_2 (out_2[2], A[2]);
  buf buffer_3 (out_2[1], A[1]);
  buf buffer_4 (out_2[0], A[0]);
endmodule

module subtr_1b (
);


  // Notes on the sheet:
  //   LF - Subtractor 1b
endmodule

module subtr_4b (
  input  [3:0] A,
  input  [3:0] B,
  output [3:0] S
);

  wire [3:0] adder_4b_1__16_8_4_2_1, nand_4b_1_s;

  LED A3 (.in(A[3]));
  LED B3 (.in(B[3]));
  LED A0 (.in(A[0]));
  LED A1 (.in(A[1]));
  LED A2 (.in(A[2]));
  LED B0 (.in(B[0]));
  LED B1 (.in(B[1]));
  LED B2 (.in(B[2]));
  LED S0 (.in(S[0]));
  LED S1 (.in(S[1]));
  LED S2 (.in(S[2]));
  LED S3 (.in(S[3]));
  adder_4b adder_4b_1 (.BusB(nand_4b_1_s), .BusA(A), ._16_8_4_2_1(adder_4b_1__16_8_4_2_1));
  nand_4b nand_4b_1 (.B(B), .A(B), .S(nand_4b_1_s));
  adder_4b adder_4b_2 (.BusB(adder_4b_1__16_8_4_2_1), .BusA(4'b0001), ._16_8_4_2_1(S));

  // Notes on the sheet:
  //   8 4 2 1
  //   8 4 2 1
  //   ...
  //   LF - Subtr 4b
  //    8 4 2 1
endmodule

module nand_4b (
  input  [3:0] A,
  input  [3:0] B,
  output [3:0] S
);

  LED A3 (.in(A[3]));
  LED B3 (.in(B[3]));
  LED A0 (.in(A[0]));
  LED A1 (.in(A[1]));
  LED A2 (.in(A[2]));
  LED B0 (.in(B[0]));
  LED B1 (.in(B[1]));
  LED B2 (.in(B[2]));
  LED S0 (.in(S[0]));
  LED S1 (.in(S[1]));
  LED S2 (.in(S[2]));
  LED S3 (.in(S[3]));
  nand nand_1 (S[0], A[0], B[0]);
  nand nand_2 (S[1], A[1], B[1]);
  nand nand_3 (S[2], A[2], B[2]);
  nand nand_4 (S[3], A[3], B[3]);

  // Notes on the sheet:
  //   8 4 2 1
  //   8 4 2 1
  //   LF - Nand 4b
  //   16 8 4 2 1
endmodule
