// Logisim project processador-ula.circ as structural Verilog
module adder_1b (
  input  A,
  input  CI,
  input  B,
  output S,
  output CO
);

  wire and_1_out, and_2_out, xor_1_out;

  xor xor_1 (xor_1_out, A, B);
  and and_1 (and_1_out, A, B);
  xor xor_2 (S, CI, xor_1_out);
  and and_2 (and_2_out, xor_1_out, CI);
  or or_1 (CO, and_2_out, and_1_out);

  // Notes on the sheet:
  //   LF - Adder 1b
endmodule

module adder_4b (
  input  [3:0] BusA,
  input  [3:0] BusB,
  output [3:0] OutS
);

  wire adder_1b_1_co, adder_1b_2_co, adder_1b_3_co, adder_1b_4_co;

  LED A3 (.in(BusA[3]));
  LED B3 (.in(BusB[3]));
  LED cO (.in(adder_1b_1_co));
  LED A0 (.in(BusA[0]));
  LED A1 (.in(BusA[1]));
  LED A2 (.in(BusA[2]));
  LED B0 (.in(BusB[0]));
  LED B1 (.in(BusB[1]));
  LED B2 (.in(BusB[2]));
  LED S0 (.in(OutS[0]));
  LED S1 (.in(OutS[1]));
  LED S2 (.in(OutS[2]));
  LED S3 (.in(OutS[3]));
  adder_1b adder_1b_1 (.CI(adder_1b_2_co), .A(BusA[3]), .B(BusB[3]), .S(OutS[3]), .CO(adder_1b_1_co));
  adder_1b adder_1b_2 (.CI(adder_1b_3_co), .A(BusA[2]), .B(BusB[2]), .S(OutS[2]), .CO(adder_1b_2_co));
  adder_1b adder_1b_3 (.CI(adder_1b_4_co), .A(BusA[1]), .B(BusB[1]), .S(OutS[1]), .CO(adder_1b_3_co));
  adder_1b adder_1b_4 (.A(BusA[0]), .B(BusB[0]), .S(OutS[0]), .CO(adder_1b_4_co));  // open: CI

  // Notes on the sheet:
  //   8 4 2 1
  //   8 4 2 1
  //   LF - Adder 4b
  //   8 4 2 1
endmodule

module ula_8op_4b (
  input  [3:0] A,
  input  [3:0] B,
  input  [2:0] Op,
  output [3:0] out_4
);

  wire [3:0] adder_4b_1_outs, divider_1_out, multiplexer_1_out, multiplier_1_out, nand_1_out, nor_1_out,
       subtractor_1_out, xnor_1_out, xor_1_out;

  adder_4b adder_4b_1 (.BusB(B), .BusA(A), .OutS(adder_4b_1_outs));
  Subtractor #(.width(4)) subtractor_1 (.a(A), .b(B), .out(subtractor_1_out));  // open: bin, bout
  Multiplier #(.width(4)) multiplier_1 (.a(A), .b(B), .out(multiplier_1_out));  // open: cin, cout
  Divider #(.width(4)) divider_1 (.a(A), .b(B), .out(divider_1_out));  // open: upper, rem
  assign nand_1_out = ~(A & B);  // NAND_Gate nand_1, 4 bits wide
  assign xor_1_out = A ^ B;  // XOR_Gate xor_1, 4 bits wide
  assign nor_1_out = ~(A | B);  // NOR_Gate nor_1, 4 bits wide
  assign xnor_1_out = ~(A ^ B);  // XNOR_Gate xnor_1, 4 bits wide
  Multiplexer #(.select(3), .width(4)) multiplexer_1 (
    .in0(4'b0000), .in1(4'b0001), .in2(4'b0010), .in3(4'b0011), .in4(4'b0100), .in5(4'b0101), .in6(4'b0110),
    .in7(4'b0111), .out(multiplexer_1_out), .sel(Op));
  Multiplexer #(.select(3), .width(4)) multiplexer_2 (
    .in0(adder_4b_1_outs), .in1(subtractor_1_out), .in2(multiplier_1_out), .in3(divider_1_out),
    .in4(nand_1_out), .in5(xor_1_out), .in6(nor_1_out), .in7(xnor_1_out), .out(out_4), .sel(Op));
  Hex_Digit_Display hex_digit_display_1 (.value(multiplexer_1_out));  // open: dp
  Hex_Digit_Display hex_digit_display_2 (.value(out_4));  // open: dp

  // Other names for the same wires on the sheet: opTest[2:0] = Op
endmodule

module subtr_4b (
  input  [3:0] BusA,
  input  [3:0] BusB,
  output [3:0] OutS
);

  LED A3 (.in(BusA[3]));
  LED B3 (.in(BusB[3]));
  LED cO ();  // open: in
  LED A0 (.in(BusA[0]));
  LED A1 (.in(BusA[1]));
  LED A2 (.in(BusA[2]));
  LED B0 (.in(BusB[0]));
  LED B1 (.in(BusB[1]));
  LED B2 (.in(BusB[2]));
  LED S0 (.in(OutS[0]));
  LED S1 (.in(OutS[1]));
  LED S2 (.in(OutS[2]));
  LED S3 (.in(OutS[3]));

  // Notes on the sheet:
  //   8 4 2 1
  //   8 4 2 1
  //   LF - Subtractor 4b
  //   8 4 2 1
endmodule

module subtr_1b (
  input  A,
  input  B,
  input  CI,
  output CO,
  output S
);


  // Notes on the sheet:
  //   LF - Subtractor 1b
endmodule
