// Logisim project processador_internet.circ as structural Verilog
module main (
);


  // Notes on the sheet:
  //   https://circuitverse.org/users/215952/projects/1-bit-half-adder-circuit
endmodule

module adder_half (
  input  A,
  input  B,
  output S,
  output C
);

  xor xor_1 (S, A, B);
  and and_1 (C, A, B);

  // Notes on the sheet:
  //   aH | S = A⊕B
  //   OaH | C = A.B
endmodule

module adder_1b (
  input  A,
  input  B,
  input  Cin,
  output S,
  output Cout
);

  wire adder_half_1_c, adder_half_1_s, adder_half_2_c;

  adder_half adder_half_1 (.A(A), .B(B), .C(adder_half_1_c), .S(adder_half_1_s));
  adder_half adder_half_2 (.A(adder_half_1_s), .B(Cin), .C(adder_half_2_c), .S(S));
  or or_1 (Cout, adder_half_2_c, adder_half_1_c);
endmodule

module adder_4b (
  input  [3:0] A,
  input  [3:0] B,
  output Cout,
  output [3:0] S
);

  wire adder_1b_2_cout, adder_1b_3_cout, adder_half_1_c;

  adder_1b adder_1b_1 (.A(A[3]), .B(B[3]), .Cin(adder_1b_2_cout), .Cout(Cout), .S(S[3]));
  adder_1b adder_1b_2 (.A(A[2]), .B(B[2]), .Cin(adder_1b_3_cout), .Cout(adder_1b_2_cout), .S(S[2]));
  adder_1b adder_1b_3 (.A(A[1]), .B(B[1]), .Cin(adder_half_1_c), .Cout(adder_1b_3_cout), .S(S[1]));
  Hex_Digit_Display hex_digit_display_1 (.value(A));  // open: dp
  adder_half adder_half_1 (.A(A[0]), .B(B[0]), .C(adder_half_1_c), .S(S[0]));
  Hex_Digit_Display hex_digit_display_2 (.value(B));  // open: dp
  Hex_Digit_Display hex_digit_display_3 (.value(S));  // open: dp

  // Other names for the same wires on the sheet: lA[3:0] = A; lB[3:0] = B; lS[3:0] = S; s4 = Cout

  // Notes on the sheet:
  //   +
  //   =
endmodule

module subtractor_4b (
  input  [3:0] A,
  input  [3:0] B,
  output [3:0] S
);

  wire adder_1b_1_cout, adder_1b_2_cout, adder_1b_3_cout, adder_1b_4_cout, not_1_out, not_2_out, not_3_out,
       not_4_out;

  not not_1 (not_1_out, B[0]);
  not not_2 (not_2_out, B[1]);
  not not_3 (not_3_out, B[2]);
  not not_4 (not_4_out, B[3]);
  LED led_1 (.in(adder_1b_1_cout));
  adder_1b adder_1b_1 (.A(A[3]), .B(not_4_out), .Cin(adder_1b_2_cout), .Cout(adder_1b_1_cout), .S(S[3]));
  adder_1b adder_1b_2 (.A(A[2]), .B(not_3_out), .Cin(adder_1b_3_cout), .Cout(adder_1b_2_cout), .S(S[2]));
  Hex_Digit_Display hex_digit_display_1 (.value(A));  // open: dp
  adder_1b adder_1b_3 (.A(A[1]), .B(not_2_out), .Cin(adder_1b_4_cout), .Cout(adder_1b_3_cout), .S(S[1]));
  Hex_Digit_Display hex_digit_display_2 (.value(B));  // open: dp
  adder_1b adder_1b_4 (.A(A[0]), .B(not_1_out), .Cin(1'b1), .Cout(adder_1b_4_cout), .S(S[0]));
  Hex_Digit_Display hex_digit_display_3 (.value(S));  // open: dp

  // Other names for the same wires on the sheet: lA[3:0] = A; lB[3:0] = B; lS[3:0] = S

  // Notes on the sheet:
  //   -
  //   =
endmodule
