// Logisim project G9_ALU_8op4b.circ as structural Verilog: 14 circuits, main circuit ALU_4b8op
module ALU_4b8op (
  input  [3:0] A,
  input  [3:0] B,
  input  [2:0] op,
  output [3:0] Q
);

  wire [3:0] adder_4b_1_q, divider_4b_logisim_1_q, multiplier_4b_1_q, nand_4b_1_q, nor_4b_1_q,
       subtractor_4b_1_q, xnor_4b_1_q, xor_4b_1_q;

  Adder_4b adder_4b_1 (.A(A), .B(B), .Q(adder_4b_1_q));  // open: Ci, Co
  Divider_4b_Logisim divider_4b_logisim_1 (.B(B), .A(A), .Q(divider_4b_logisim_1_q));  // open: Upper, Rems
  Multiplier_4b multiplier_4b_1 (.A(A), .B(B), .Q(multiplier_4b_1_q));  // open: Cin, Co
  Nand_4b nand_4b_1 (.A(A), .B(B), .Q(nand_4b_1_q));
  Nor_4b nor_4b_1 (.A(A), .B(B), .Q(nor_4b_1_q));
  Subtractor_4b subtractor_4b_1 (.B(B), .A(A), .Q(subtractor_4b_1_q));  // open: Bo
  Xor_4b xor_4b_1 (.A(A), .B(B), .Q(xor_4b_1_q));
  Xnor_4b xnor_4b_1 (.A(A), .B(B), .Q(xnor_4b_1_q));
  Hex_Digit_Display hex_digit_display_1 (.value(A));  // open: dp
  Multiplexador_8op_4b multiplexador_8op_4b_1 (
    .E(nor_4b_1_q), .B(divider_4b_logisim_1_q), .F(subtractor_4b_1_q), .C(multiplier_4b_1_q),
    .G(xnor_4b_1_q), .D(nand_4b_1_q), .H(xor_4b_1_q), .op(op), .A(adder_4b_1_q), .Q(Q));
  Hex_Digit_Display hex_digit_display_2 (.value(B));  // open: dp
  Hex_Digit_Display hex_digit_display_3 (.value({1'b0, op}));  // open: dp
  Hex_Digit_Display hex_digit_display_4 (.value(Q));  // open: dp

  // Other names for the same wires on the sheet: TN_A[3:0] = A; TN_B[3:0] = B; TN_Op[2:0] = op; TN_Q[3:0] = Q
endmodule

module Adder_Half (
  input  A,
  input  B,
  output Q,
  output Co
);

  xor xor_1 (Q, A, B);
  and and_1 (Co, A, B);

  // Notes on the sheet:
  //   Q = A ⊕ B
  //   Co = A • B
endmodule

module Adder_Full_1b (
  input  A,
  input  B,
  input  Ci,
  output Co,
  output Q
);

  wire adder_half_1_co, adder_half_1_q, adder_half_2_co;

  Adder_Half adder_half_1 (.A(A), .B(B), .Q(adder_half_1_q), .Co(adder_half_1_co));
  Adder_Half adder_half_2 (.A(adder_half_1_q), .B(Ci), .Q(Q), .Co(adder_half_2_co));
  or or_1 (Co, adder_half_2_co, adder_half_1_co);

  // Notes on the sheet:
  //   Q = A ⊕ B ⊕ Ci
  //   Co ​= ( A • B ) + ( Ci​ • ( A ⊕ B ) )
  //   T1 = A ⊕ B
  //   T2 = A • B
  //   T3 = Ci • T1
  //   Q = T1 ⊕ Ci
  //   Co ​= T2 + T3
endmodule

module Adder_4b (
  input  [3:0] A,
  input  [3:0] B,
  input  Ci,
  output Co,
  output [3:0] Q
);

  wire adder_full_1b_1_co, adder_full_1b_2_co, adder_full_1b_3_co;

  Adder_Full_1b adder_full_1b_1 (.Ci(Ci), .A(A[0]), .B(B[0]), .Co(adder_full_1b_1_co), .Q(Q[0]));
  Adder_Full_1b adder_full_1b_2 (.Ci(adder_full_1b_1_co), .A(A[1]), .B(B[1]), .Co(adder_full_1b_2_co), .Q(Q[1]));
  Adder_Full_1b adder_full_1b_3 (.Ci(adder_full_1b_2_co), .A(A[2]), .B(B[2]), .Co(adder_full_1b_3_co), .Q(Q[2]));
  Adder_Full_1b adder_full_1b_4 (.Ci(adder_full_1b_3_co), .A(A[3]), .B(B[3]), .Co(Co), .Q(Q[3]));
endmodule

module Subtractor_4b (
  input  [3:0] A,
  input  [3:0] B,
  output [3:0] Q,
  output Bo
);

  wire [3:0] nand_4b_1_q;

  Nand_4b nand_4b_1 (.A(B), .B(B), .Q(nand_4b_1_q));
  Adder_4b adder_4b_1 (.A(A), .B(nand_4b_1_q), .Ci(1'b1), .Co(Bo), .Q(Q));
endmodule

module Multiplier_2b_Pure (
  input  [1:0] A,
  input  [1:0] B,
  output [1:0] Q,
  output [1:0] Co
);

  wire and_2_out, and_3_out, and_4_out, and_5_out;

  Hex_Digit_Display hex_digit_display_1 (.value({2'b00, A}));  // open: dp
  Hex_Digit_Display hex_digit_display_2 (.value({2'b00, B}));  // open: dp
  and and_1 (Q[0], A[0], B[0]);
  and and_2 (and_2_out, A[1], B[0]);
  and and_3 (and_3_out, A[0], B[1]);
  and and_4 (and_4_out, A[1], B[1]);
  xor xor_1 (Q[1], and_2_out, and_3_out);
  and and_5 (and_5_out, and_2_out, and_3_out);
  xor xor_2 (Co[0], and_5_out, and_4_out);
  and and_6 (Co[1], and_5_out, and_4_out);
  Hex_Digit_Display hex_digit_display_3 (.value({Co, Q}));  // open: dp
endmodule

module Multiplier_2b (
  input  [1:0] A,
  input  [1:0] B,
  output [1:0] Q,
  output [1:0] Co
);

  wire adder_half_1_co, W1_out, W2_out, W3_out;

  Hex_Digit_Display hex_digit_display_1 (.value({2'b00, A}));  // open: dp
  Hex_Digit_Display hex_digit_display_2 (.value({2'b00, B}));  // open: dp
  and P0 (Q[0], A[0], B[0]);
  and W1 (W1_out, A[1], B[0]);
  and W2 (W2_out, A[0], B[1]);
  and W3 (W3_out, A[1], B[1]);
  Adder_Half adder_half_1 (.A(W1_out), .B(W2_out), .Q(Q[1]), .Co(adder_half_1_co));
  Hex_Digit_Display hex_digit_display_3 (.value({Co, Q}));  // open: dp
  Adder_Half adder_half_2 (.A(adder_half_1_co), .B(W3_out), .Q(Co[0]), .Co(Co[1]));
endmodule

module Multiplier_4b (
  input  [3:0] A,
  input  Cin,
  input  [3:0] B,
  output [3:0] Co,
  output [3:0] Q
);

  wire [2:0] and_15_out;
  wire [3:0] adder_4b_2_co, adder_4b_3_co, and_10_out, and_11_out, and_12_out;

  and and_1 (and_10_out[3], A[3], B[1]);
  and and_2 (and_11_out[3], A[3], B[2]);
  and and_3 (and_12_out[3], A[3], B[3]);
  and and_4 (and_10_out[2], A[2], B[1]);
  and and_5 (and_10_out[1], B[1], A[1]);
  and and_6 (and_11_out[2], A[2], B[2]);
  and and_7 (and_11_out[1], B[2], A[1]);
  and and_8 (and_12_out[2], A[2], B[3]);
  and and_9 (and_12_out[1], B[3], A[1]);
  and and_10 (and_10_out[0], B[1], A[0]);
  and and_11 (and_11_out[0], B[2], A[0]);
  and and_12 (and_12_out[0], B[3], A[0]);
  Adder_4b adder_4b_1 (.A(adder_4b_2_co), .B(and_12_out), .Co(Co[3]), .Q({Co[2:0], Q[3]}));  // open: Ci
  Adder_4b adder_4b_2 (
    .A(adder_4b_3_co), .B(and_11_out), .Co(adder_4b_2_co[3]), .Q({adder_4b_2_co[2:0], Q[2]}));  // open: Ci
  Adder_4b adder_4b_3 (
    .A({Cin, and_15_out}), .B(and_10_out), .Co(adder_4b_3_co[3]), .Q({adder_4b_3_co[2:0], Q[1]}));  // open: Ci
  and and_13 (and_15_out[2], A[3], B[0]);
  and and_14 (and_15_out[1], A[2], B[0]);
  and and_15 (and_15_out[0], B[0], A[1]);
  and and_16 (Q[0], B[0], A[0]);
  Hex_Digit_Display hex_digit_display_1 (.value(A));  // open: dp
  // Probe on A
  Hex_Digit_Display hex_digit_display_2 (.value(B));  // open: dp
  // Probe on B
  Hex_Digit_Display hex_digit_display_3 (.value(Co));  // open: dp
  Hex_Digit_Display hex_digit_display_4 (.value(Q));  // open: dp
  // Probe on Co
  // Probe on Q

  // Other names for the same wires on the sheet: QT[3:0] = Q; CoT[3:0] = Co; AT[3:0] = A; BT[3:0] = B
endmodule

module Multiplier_4b_Logisim (
  input  [3:0] Ci,
  input  [3:0] A,
  input  [3:0] B,
  output [3:0] Q,
  output [3:0] Co
);

  Multiplier #(.width(4)) multiplier_1 (.a(A), .b(B), .out(Q), .cin(Ci), .cout(Co));
endmodule

module Divider_4b_Logisim (
  input  [3:0] Upper,
  input  [3:0] A,
  input  [3:0] B,
  output [3:0] Q,
  output [3:0] Rems
);

  Divider #(.width(4)) divider_1 (.a(A), .b(B), .out(Q), .upper(Upper), .rem(Rems));
endmodule

module Nand_4b (
  input  [3:0] A,
  input  [3:0] B,
  output [3:0] Q
);

  nand nand_1 (Q[0], A[0], B[0]);
  nand nand_2 (Q[1], A[1], B[1]);
  nand nand_3 (Q[2], A[2], B[2]);
  nand nand_4 (Q[3], A[3], B[3]);
endmodule

module Nor_4b (
  input  [3:0] A,
  input  [3:0] B,
  output [3:0] Q
);

  nor nor_1 (Q[0], A[0], B[0]);
  nor nor_2 (Q[1], A[1], B[1]);
  nor nor_3 (Q[2], A[2], B[2]);
  nor nor_4 (Q[3], A[3], B[3]);
endmodule

module Xor_4b (
  input  [3:0] A,
  input  [3:0] B,
  output [3:0] Q
);

  xor xor_1 (Q[0], A[0], B[0]);
  xor xor_2 (Q[1], A[1], B[1]);
  xor xor_3 (Q[2], A[2], B[2]);
  xor xor_4 (Q[3], A[3], B[3]);
endmodule

module Xnor_4b (
  input  [3:0] A,
  input  [3:0] B,
  output [3:0] Q
);

  xnor xnor_1 (Q[0], A[0], B[0]);
  xnor xnor_2 (Q[1], A[1], B[1]);
  xnor xnor_3 (Q[2], A[2], B[2]);
  xnor xnor_4 (Q[3], A[3], B[3]);
endmodule
