// Logisim project G9_CPU.circ as structural Verilog: 7 circuits, main circuit CPU
module CPU (
  input  E4,
  input  E3,
  input  E2,
  input  E1,
  input  E0,
  input  T3,
  input  T2,
  input  T1,
  input  T0,
  output [3:0] S
);

  wire CLK_LATCH_out, CLK_MAR_out, CLK_MBR_REGISTERS_out, CLK_MIR_out, mir_1_q0, mir_1_q1, mir_1_q2,
       mir_1_q3, mir_1_q4, mir_1_q5, mir_1_q6, mir_1_q7, mir_1_q8, mir_1_q9, mir_1_q10, mir_1_q11, mir_1_q12,
       mir_1_q13, mir_1_q19, mir_bank_1_q0, mir_bank_1_q1, mir_bank_1_q2, mir_bank_1_q3, mir_bank_1_q4,
       mir_bank_1_q5, mir_bank_1_q6, mir_bank_1_q7, mir_bank_1_q8, mir_bank_1_q9, mir_bank_1_q10,
       mir_bank_1_q11, mir_bank_1_q12, mir_bank_1_q13, mir_bank_1_q14, mir_bank_1_q15, mir_bank_1_q16,
       mir_bank_1_q17, mir_bank_1_q18, mir_bank_1_q19, mir_bank_1_q20, mir_bank_1_q21, mir_bank_1_q22,
       mir_bank_1_q23;
  wire [1:0] mir_1_q14;
  wire [2:0] mir_1_q16;
  wire [3:0] a_multiplexador_2op_4b_1_q, alu_4b8op_1_q, latch_4b_1_q, latch_4b_2_q, mbr_4b_1_q,
       mbr_4b_1_srxtx, register_bank_4b_1_a, register_bank_4b_1_b, rxtx_1_sext, shifter_3op_4b_1_q;

  Hex_Digit_Display hex_digit_display_1 (.value({T3, T2, T1, T0}));  // open: dp
  Hex_Digit_Display hex_digit_display_2 (.value(S));  // open: dp
  RxTx rxtx_1 (.T_R(mir_1_q10), .BusExt(mbr_4b_1_srxtx), .TEC({T3, T2, T1, T0}), .DIS(S), .SExt(rxtx_1_sext));
  MAR_4b mar_4b_1 (.D(latch_4b_2_q), .Clock(CLK_MAR_out), .E(mir_1_q13));  // open: R, Q, Qn
  Hex_Digit_Display hex_digit_display_3 (.value(rxtx_1_sext));  // open: dp
  Hex_Digit_Display hex_digit_display_4 (.value(mbr_4b_1_srxtx));  // open: dp
  Clock #(.lowDuration(3), .phaseOffset(3)) CLK_MIR (.out(CLK_MIR_out));
  Clock #(.lowDuration(3), .phaseOffset(2)) CLK_LATCH (.out(CLK_LATCH_out));
  Clock #(.lowDuration(3), .phaseOffset(1)) CLK_MAR (.out(CLK_MAR_out));
  Clock #(.lowDuration(3)) CLK_MBR_REGISTERS (.out(CLK_MBR_REGISTERS_out));
  Hex_Digit_Display hex_digit_display_5 (.value(shifter_3op_4b_1_q));  // open: dp
  MBR_4b mbr_4b_1 (
    .Clk(CLK_MBR_REGISTERS_out), .E(mir_1_q12), .ERxTx(rxtx_1_sext), .D(shifter_3op_4b_1_q), .Wr(mir_1_q10),
    .Rd(mir_1_q11), .Q(mbr_4b_1_q), .SRxTx(mbr_4b_1_srxtx));  // open: SnRxTx, Qn
  Hex_Digit_Display hex_digit_display_6 (.value(latch_4b_2_q));  // open: dp
  Hex_Digit_Display hex_digit_display_7 (.value(mbr_4b_1_q));  // open: dp
  Register_Bank_4b register_bank_4b_1 (
    .D(shifter_3op_4b_1_q), .C2(mir_1_q8), .C1(mir_1_q7), .C0(mir_1_q6), .Clk(CLK_MBR_REGISTERS_out),
    .E(mir_1_q9), .A2(mir_1_q5), .A1(mir_1_q4), .A0(mir_1_q3), .B2(mir_1_q2), .B1(mir_1_q1), .B0(mir_1_q0),
    .A(register_bank_4b_1_a), .B(register_bank_4b_1_b));
  Shifter_3op_4b shifter_3op_4b_1 (.U(alu_4b8op_1_q), .op(mir_1_q14), .Q(shifter_3op_4b_1_q));
  Latch_4b latch_4b_1 (.D(register_bank_4b_1_a), .E(CLK_LATCH_out), .Q(latch_4b_1_q));  // open: R, Qn
  A_Multiplexador_2op_4b a_multiplexador_2op_4b_1 (
    .B(mbr_4b_1_q), .op(mir_1_q19), .A(latch_4b_1_q), .Q(a_multiplexador_2op_4b_1_q));
  ALU_4b8op alu_4b8op_1 (.A(a_multiplexador_2op_4b_1_q), .B(latch_4b_2_q), .op(mir_1_q16), .Q(alu_4b8op_1_q));
  Latch_4b latch_4b_2 (.D(register_bank_4b_1_b), .E(CLK_LATCH_out), .Q(latch_4b_2_q));  // open: R, Qn
  MIR_Bank mir_bank_1 (
    .E4(E4), .E3(E3), .E2(E2), .E1(E1), .E0(E0), .Q0(mir_bank_1_q0), .Q1(mir_bank_1_q1), .Q2(mir_bank_1_q2),
    .Q3(mir_bank_1_q3), .Q4(mir_bank_1_q4), .Q5(mir_bank_1_q5), .Q6(mir_bank_1_q6), .Q7(mir_bank_1_q7),
    .Q8(mir_bank_1_q8), .Q9(mir_bank_1_q9), .Q10(mir_bank_1_q10), .Q11(mir_bank_1_q11), .Q12(mir_bank_1_q12),
    .Q13(mir_bank_1_q13), .Q14(mir_bank_1_q14), .Q15(mir_bank_1_q15), .Q16(mir_bank_1_q16),
    .Q17(mir_bank_1_q17), .Q18(mir_bank_1_q18), .Q19(mir_bank_1_q19), .Q20(mir_bank_1_q20),
    .Q21(mir_bank_1_q21), .Q22(mir_bank_1_q22), .Q23(mir_bank_1_q23));
  MIR mir_1 (
    .MBR(mir_bank_1_q12), .MAR(mir_bank_1_q13), .SH0(mir_bank_1_q14), .SH1(mir_bank_1_q15),
    .ALU0(mir_bank_1_q16), .ALU1(mir_bank_1_q17), .ALU2(mir_bank_1_q18), .AMUX(mir_bank_1_q19),
    .X0(mir_bank_1_q20), .DEC_B1(mir_bank_1_q1), .X1(mir_bank_1_q21), .X2(mir_bank_1_q22),
    .X3(mir_bank_1_q23), .DEC_B2(mir_bank_1_q2), .DEC_A0(mir_bank_1_q3), .DEC_A1(mir_bank_1_q4),
    .DEC_A2(mir_bank_1_q5), .DEC_C0(mir_bank_1_q6), .DEC_C1(mir_bank_1_q7), .DEC_C2(mir_bank_1_q8),
    .BR(mir_bank_1_q9), .Wr(mir_bank_1_q10), .DEC_B0(mir_bank_1_q0), .Rd(mir_bank_1_q11), .Clk(CLK_MIR_out),
    .Q12(mir_1_q12), .Q13(mir_1_q13), .Q14(mir_1_q14[0]), .Q15(mir_1_q14[1]), .Q16(mir_1_q16[0]),
    .Q17(mir_1_q16[1]), .Q18(mir_1_q16[2]), .Q19(mir_1_q19), .Q1(mir_1_q1), .Q2(mir_1_q2), .Q3(mir_1_q3),
    .Q4(mir_1_q4), .Q5(mir_1_q5), .Q6(mir_1_q6), .Q7(mir_1_q7), .Q8(mir_1_q8), .Q9(mir_1_q9),
    .Q10(mir_1_q10), .Q0(mir_1_q0), .Q11(mir_1_q11));  // open: Q20, Q21, Q22, Q23
endmodule

module CPU_NoMIRBank (
  input  in_1,
  input  in_2,
  input  in_3,
  input  in_4,
  input  in_5,
  input  in_6,
  input  in_7,
  input  in_8,
  input  in_9,
  input  in_10,
  input  in_11,
  input  in_12,
  input  in_13,
  input  in_14,
  input  in_15,
  input  in_16,
  input  in_17,
  input  in_18,
  input  in_19,
  input  in_20,
  input  T3,
  input  T2,
  input  T1,
  input  T0,
  output [3:0] S
);

  wire CLK_LATCH_out, CLK_MAR_out, CLK_MBR_REGISTERS_out, CLK_MIR_out, mir_1_q0, mir_1_q1, mir_1_q2,
       mir_1_q3, mir_1_q4, mir_1_q5, mir_1_q6, mir_1_q7, mir_1_q8, mir_1_q9, mir_1_q10, mir_1_q11, mir_1_q12,
       mir_1_q13, mir_1_q19, or_1_out;
  wire [1:0] mir_1_q14;
  wire [2:0] mir_1_q16;
  wire [3:0] a_multiplexador_2op_4b_1_q, alu_4b8op_1_q, latch_4b_1_q, latch_4b_2_q, mar_4b_1_q, mbr_4b_1_q,
       mbr_4b_1_srxtx, register_bank_4b_1_a, register_bank_4b_1_b, rxtx_1_sext, shifter_3op_4b_1_q;

  Hex_Digit_Display hex_digit_display_1 (.value({T3, T2, T1, T0}));  // open: dp
  Hex_Digit_Display hex_digit_display_2 (.value(S));  // open: dp
  RxTx rxtx_1 (.T_R(or_1_out), .BusExt(mbr_4b_1_srxtx), .TEC({T3, T2, T1, T0}), .DIS(S), .SExt(rxtx_1_sext));
  or or_1 (or_1_out, mar_4b_1_q[3], mar_4b_1_q[2], mar_4b_1_q[1], mar_4b_1_q[0]);
  MAR_4b mar_4b_1 (.D(latch_4b_2_q), .Clock(CLK_MAR_out), .E(mir_1_q13), .Q(mar_4b_1_q));  // open: R, Qn
  Hex_Digit_Display hex_digit_display_3 (.value(rxtx_1_sext));  // open: dp
  Hex_Digit_Display hex_digit_display_4 (.value(mbr_4b_1_srxtx));  // open: dp
  Clock #(.lowDuration(3), .phaseOffset(3)) CLK_MIR (.out(CLK_MIR_out));
  Clock #(.lowDuration(3), .phaseOffset(2)) CLK_LATCH (.out(CLK_LATCH_out));
  Clock #(.lowDuration(3), .phaseOffset(1)) CLK_MAR (.out(CLK_MAR_out));
  Clock #(.lowDuration(3)) CLK_MBR_REGISTERS (.out(CLK_MBR_REGISTERS_out));
  Hex_Digit_Display hex_digit_display_5 (.value(shifter_3op_4b_1_q));  // open: dp
  MBR_4b mbr_4b_1 (
    .Clk(CLK_MBR_REGISTERS_out), .E(mir_1_q12), .ERxTx(rxtx_1_sext), .D(shifter_3op_4b_1_q), .Wr(mir_1_q10),
    .Rd(mir_1_q11), .Q(mbr_4b_1_q), .SRxTx(mbr_4b_1_srxtx));  // open: SnRxTx, Qn
  Hex_Digit_Display hex_digit_display_6 (.value(latch_4b_2_q));  // open: dp
  Hex_Digit_Display hex_digit_display_7 (.value(mbr_4b_1_q));  // open: dp
  Register_Bank_4b register_bank_4b_1 (
    .D(shifter_3op_4b_1_q), .C2(mir_1_q8), .C1(mir_1_q7), .C0(mir_1_q6), .Clk(CLK_MBR_REGISTERS_out),
    .E(mir_1_q9), .A2(mir_1_q5), .A1(mir_1_q4), .A0(mir_1_q3), .B2(mir_1_q2), .B1(mir_1_q1), .B0(mir_1_q0),
    .A(register_bank_4b_1_a), .B(register_bank_4b_1_b));
  Shifter_3op_4b shifter_3op_4b_1 (.U(alu_4b8op_1_q), .op(mir_1_q14), .Q(shifter_3op_4b_1_q));
  Latch_4b latch_4b_1 (.D(register_bank_4b_1_a), .E(CLK_LATCH_out), .Q(latch_4b_1_q));  // open: R, Qn
  A_Multiplexador_2op_4b a_multiplexador_2op_4b_1 (
    .B(mbr_4b_1_q), .op(mir_1_q19), .A(latch_4b_1_q), .Q(a_multiplexador_2op_4b_1_q));
  ALU_4b8op alu_4b8op_1 (.A(a_multiplexador_2op_4b_1_q), .B(latch_4b_2_q), .op(mir_1_q16), .Q(alu_4b8op_1_q));
  Hex_Digit_Display hex_digit_display_8 (.value(register_bank_4b_1_a));  // open: dp
  Latch_4b latch_4b_2 (.D(register_bank_4b_1_b), .E(CLK_LATCH_out), .Q(latch_4b_2_q));  // open: R, Qn
  Hex_Digit_Display hex_digit_display_9 (.value(register_bank_4b_1_b));  // open: dp
  MIR mir_1 (
    .MBR(in_8), .MAR(in_7), .SH0(in_6), .SH1(in_5), .ALU0(in_4), .ALU1(in_3), .ALU2(in_2), .AMUX(in_1),
    .DEC_B1(in_19), .DEC_B2(in_18), .DEC_A0(in_17), .DEC_A1(in_16), .DEC_A2(in_15), .DEC_C0(in_14),
    .DEC_C1(in_13), .DEC_C2(in_12), .BR(in_11), .Wr(in_10), .DEC_B0(in_20), .Rd(in_9), .Clk(CLK_MIR_out),
    .Q12(mir_1_q12), .Q13(mir_1_q13), .Q14(mir_1_q14[0]), .Q15(mir_1_q14[1]), .Q16(mir_1_q16[0]),
    .Q17(mir_1_q16[1]), .Q18(mir_1_q16[2]), .Q19(mir_1_q19), .Q1(mir_1_q1), .Q2(mir_1_q2), .Q3(mir_1_q3),
    .Q4(mir_1_q4), .Q5(mir_1_q5), .Q6(mir_1_q6), .Q7(mir_1_q7), .Q8(mir_1_q8), .Q9(mir_1_q9),
    .Q10(mir_1_q10), .Q0(mir_1_q0), .Q11(mir_1_q11));  // open: X0, X1, X2, X3, Q20, Q21, Q22, Q23
endmodule

module MIR (
  input  Clk,
  input  DEC_B0,
  input  DEC_B1,
  input  DEC_B2,
  input  DEC_A0,
  input  DEC_A1,
  input  DEC_A2,
  input  DEC_C0,
  input  DEC_C1,
  input  DEC_C2,
  input  BR,
  input  Wr,
  input  Rd,
  input  MBR,
  input  MAR,
  input  SH0,
  input  SH1,
  input  ALU0,
  input  ALU1,
  input  ALU2,
  input  AMUX,
  input  X0,
  input  X1,
  input  X2,
  input  X3,
  output Q0,
  output Q1,
  output Q2,
  output Q3,
  output Q4,
  output Q5,
  output Q6,
  output Q7,
  output Q8,
  output Q9,
  output Q10,
  output Q11,
  output Q12,
  output Q13,
  output Q14,
  output Q15,
  output Q16,
  output Q17,
  output Q18,
  output Q19,
  output Q20,
  output Q21,
  output Q22,
  output Q23
);

  wire undriven;

  D_Flip_Flop d_ff_1 (.D(DEC_B0), .clk(Clk), .Q(Q0));  // open: Qn, preset, reset
  D_Flip_Flop d_ff_2 (.D(DEC_B1), .clk(Clk), .Q(Q1));  // open: Qn, preset, reset
  D_Flip_Flop d_ff_3 (.D(DEC_B2), .clk(Clk), .Q(Q2));  // open: Qn, preset, reset
  D_Flip_Flop d_ff_4 (.D(DEC_A0), .clk(Clk), .Q(Q3));  // open: Qn, preset, reset
  D_Flip_Flop d_ff_5 (.D(DEC_A1), .clk(Clk), .Q(Q4));  // open: Qn, preset, reset
  D_Flip_Flop d_ff_6 (.D(DEC_A2), .clk(Clk), .Q(Q5));  // open: Qn, preset, reset
  D_Flip_Flop d_ff_7 (.D(DEC_C0), .clk(Clk), .Q(Q6));  // open: Qn, preset, reset
  D_Flip_Flop d_ff_8 (.D(DEC_C1), .clk(Clk), .Q(Q7));  // open: Qn, preset, reset
  D_Flip_Flop d_ff_9 (.D(DEC_C2), .clk(Clk), .Q(Q8));  // open: Qn, preset, reset
  D_Flip_Flop d_ff_10 (.D(BR), .clk(Clk), .Q(Q9));  // open: Qn, preset, reset
  D_Flip_Flop d_ff_11 (.D(Wr), .clk(Clk), .Q(Q10));  // open: Qn, preset, reset
  D_Flip_Flop d_ff_12 (.D(Rd), .clk(Clk), .Q(Q11));  // open: Qn, preset, reset
  D_Flip_Flop d_ff_13 (.D(MBR), .clk(Clk), .Q(Q12));  // open: Qn, preset, reset
  D_Flip_Flop d_ff_14 (.D(MAR), .clk(Clk), .Q(Q13));  // open: Qn, preset, reset
  D_Flip_Flop d_ff_15 (.D(SH0), .clk(Clk), .Q(Q14));  // open: Qn, preset, reset
  D_Flip_Flop d_ff_16 (.D(SH1), .clk(Clk), .Q(Q15));  // open: Qn, preset, reset
  D_Flip_Flop d_ff_17 (.D(ALU0), .clk(Clk), .Q(Q16));  // open: Qn, preset, reset
  D_Flip_Flop d_ff_18 (.D(ALU1), .clk(Clk), .Q(Q17));  // open: Qn, preset, reset
  D_Flip_Flop d_ff_19 (.D(ALU2), .clk(Clk), .Q(Q18));  // open: Qn, preset, reset
  D_Flip_Flop d_ff_20 (.D(AMUX), .clk(Clk), .Q(Q19));  // open: Qn, preset, reset
  D_Flip_Flop d_ff_21 (.clk(undriven), .Q(Q20));  // open: D, Qn, preset, reset
  D_Flip_Flop d_ff_22 (.clk(undriven), .Q(Q21));  // open: D, Qn, preset, reset
  D_Flip_Flop d_ff_23 (.clk(undriven), .Q(Q22));  // open: D, Qn, preset, reset
  D_Flip_Flop d_ff_24 (.clk(undriven), .Q(Q23));  // open: D, Qn, preset, reset
endmodule

module MIR_Bank (
  input  E4,
  input  E3,
  input  E2,
  input  E1,
  input  E0,
  output Q0,
  output Q1,
  output Q2,
  output Q3,
  output Q4,
  output Q5,
  output Q6,
  output Q7,
  output Q8,
  output Q9,
  output Q10,
  output Q11,
  output Q12,
  output Q13,
  output Q14,
  output Q15,
  output Q16,
  output Q17,
  output Q18,
  output Q19,
  output Q20,
  output Q21,
  output Q22,
  output Q23
);

  ROM #(.addrWidth(5), .dataWidth(24)) ROM_32x24 (
    .addr({E4, E3, E2, E1, E0}),
    .data({Q23, Q22, Q21, Q20, Q19, Q18, Q17, Q16, Q15, Q14, Q13, Q12, Q11, Q10, Q9, Q8, Q7, Q6, Q5, Q4, Q3, Q2, Q1, Q0}));
endmodule

module RxTx (
  input  [3:0] TEC,
  input  [3:0] BusExt,
  input  T_R,
  output [3:0] DIS,
  output [3:0] SExt
);

  wire a_decoder_2op_1b_1x2_1_m0, a_decoder_2op_1b_1x2_1_m1;
  wire [3:0] buffer_tristate_ah_4b_1_q, buffer_tristate_ah_4b_2_q;

  A_Decoder_2op_1b_1x2 a_decoder_2op_1b_1x2_1 (
    .op(T_R), .m0(a_decoder_2op_1b_1x2_1_m0), .m1(a_decoder_2op_1b_1x2_1_m1));
  Buffer_TriState_AH_1b buffer_tristate_ah_1b_1 (.A(TEC[3]), .Ctrl(a_decoder_2op_1b_1x2_1_m0), .Q(SExt[3]));
  Buffer_TriState_AH_1b buffer_tristate_ah_1b_2 (.A(TEC[2]), .Ctrl(a_decoder_2op_1b_1x2_1_m0), .Q(SExt[2]));
  Buffer_TriState_AH_1b buffer_tristate_ah_1b_3 (.A(TEC[1]), .Ctrl(a_decoder_2op_1b_1x2_1_m0), .Q(SExt[1]));
  Buffer_TriState_AH_1b buffer_tristate_ah_1b_4 (.A(TEC[0]), .Ctrl(a_decoder_2op_1b_1x2_1_m0), .Q(SExt[0]));
  Buffer_TriState_AH_1b buffer_tristate_ah_1b_5 (.A(BusExt[3]), .Ctrl(a_decoder_2op_1b_1x2_1_m1), .Q(DIS[3]));
  Buffer_TriState_AH_1b buffer_tristate_ah_1b_6 (.A(BusExt[2]), .Ctrl(a_decoder_2op_1b_1x2_1_m1), .Q(DIS[2]));
  Buffer_TriState_AH_1b buffer_tristate_ah_1b_7 (.A(BusExt[1]), .Ctrl(a_decoder_2op_1b_1x2_1_m1), .Q(DIS[1]));
  Buffer_TriState_AH_1b buffer_tristate_ah_1b_8 (.A(BusExt[0]), .Ctrl(a_decoder_2op_1b_1x2_1_m1), .Q(DIS[0]));
  Buffer_TriState_AH_4b buffer_tristate_ah_4b_1 (
    .Ctrl(a_decoder_2op_1b_1x2_1_m0), .A(TEC), .Q(buffer_tristate_ah_4b_1_q));
  Buffer_TriState_AH_4b buffer_tristate_ah_4b_2 (
    .Ctrl(a_decoder_2op_1b_1x2_1_m1), .A(BusExt), .Q(buffer_tristate_ah_4b_2_q));
  Hex_Digit_Display hex_digit_display_1 (.value(buffer_tristate_ah_4b_1_q));  // open: dp
  Hex_Digit_Display hex_digit_display_2 (.value(buffer_tristate_ah_4b_2_q));  // open: dp
endmodule

module Increment (
  input  Clear,
  input  Clk,
  output [4:0] S
);

  Counter #(.max('h1f), .width(5)) counter_1 (.clr(Clear), .clk(Clk), .Q(S));  // open: load, up, count, D, carry
endmodule

module Programa (
  input  [4:0] E,
  output [4:0] out_2
);

  ROM #(.addrWidth(5), .dataWidth(5)) rom_1 (.addr(E), .data(out_2));
endmodule
