// Logisim project G9_Registers_Memorys.circ as structural Verilog: 14 circuits, main circuit Latch_Master_1b
module Latch_Master_1b (
  input  D,
  input  E,
  output Q,
  output Qn
);

  wire nand_1_out, nand_2_out, nand_3_out;

  nand nand_1 (nand_1_out, D, D);
  nand nand_2 (nand_2_out, D, E);
  nand nand_3 (nand_3_out, E, nand_1_out);
  nand nand_4 (Q, nand_2_out, Qn);
  nand nand_5 (Qn, Q, nand_3_out);

  // Notes on the sheet:
  //   E D Q Q'
  //   0 0 Hold Hold'
  //   0 1 Hold Hold'
  //   1 0 Reset Set
  //   1 1 Set Reset
  //   Tipo D
  //   D = Data
  //   E = Enable (clock)
  //   Ctrl
  //   Q' = Qn ( !Q )
  //   Memoria
endmodule

module Latch_Slave_1b (
  input  D,
  input  E,
  input  R,
  output Q,
  output Qn
);

  wire nand_1_out, nand_2_out;

  nand nand_1 (nand_1_out, D, E);
  nand nand_2 (nand_2_out, E, R);
  nand nand_3 (Q, nand_1_out, Qn);
  nand nand_4 (Qn, Q, nand_2_out);

  // Notes on the sheet:
  //   Ctrl
  //   Memoria
endmodule

module Latch_Master_4b (
  input  [3:0] D,
  input  E,
  output [3:0] Q,
  output [3:0] Qn
);

  Latch_Master_1b latch_master_1b_1 (.D(D[3]), .E(E), .Qn(Qn[3]), .Q(Q[3]));
  Latch_Master_1b latch_master_1b_2 (.D(D[2]), .E(E), .Qn(Qn[2]), .Q(Q[2]));
  Latch_Master_1b latch_master_1b_3 (.D(D[1]), .E(E), .Qn(Qn[1]), .Q(Q[1]));
  Latch_Master_1b latch_master_1b_4 (.D(D[0]), .E(E), .Qn(Qn[0]), .Q(Q[0]));
endmodule

module Latch_Slave_4b (
  input  [3:0] D,
  input  E,
  input  R,
  output [3:0] Q,
  output [3:0] Qn
);

  Latch_Slave_1b latch_slave_1b_1 (.R(R), .D(D[3]), .E(E), .Qn(Qn[3]), .Q(Q[3]));
  Latch_Slave_1b latch_slave_1b_2 (.R(R), .D(D[2]), .E(E), .Qn(Qn[2]), .Q(Q[2]));
  Latch_Slave_1b latch_slave_1b_3 (.R(R), .D(D[1]), .E(E), .Qn(Qn[1]), .Q(Q[1]));
  Latch_Slave_1b latch_slave_1b_4 (.R(R), .D(D[0]), .E(E), .Qn(Qn[0]), .Q(Q[0]));
endmodule

module FlipFlopD_1b (
  input  D,
  input  E,
  input  R,
  output Q,
  output Qn
);

  wire Master_Latcher_q, not_1_out;

  not not_1 (not_1_out, E);
  Latch_Master_1b Master_Latcher (.D(D), .E(E), .Q(Master_Latcher_q));  // open: Qn
  Latch_Slave_1b Slave_Latcher (.R(not_1_out), .D(Master_Latcher_q), .E(R), .Qn(Qn), .Q(Q));
endmodule

module FlipFlopD_4b (
  input  [3:0] D,
  input  E,
  input  R,
  output [3:0] Q,
  output [3:0] Qn
);

  FlipFlopD_1b flipflopd_1b_1 (.E(E), .R(R), .D(D[3]), .Qn(Qn[3]), .Q(Q[3]));
  FlipFlopD_1b flipflopd_1b_2 (.E(E), .R(R), .D(D[2]), .Qn(Qn[2]), .Q(Q[2]));
  FlipFlopD_1b flipflopd_1b_3 (.E(E), .R(R), .D(D[1]), .Qn(Qn[1]), .Q(Q[1]));
  FlipFlopD_1b flipflopd_1b_4 (.E(E), .R(R), .D(D[0]), .Qn(Qn[0]), .Q(Q[0]));
endmodule

module Latch_4b (
  input  [3:0] D,
  input  E,
  input  R,
  output [3:0] Q,
  output [3:0] Qn
);

  D_Flip_Flop d_ff_1 (.D(D[0]), .clk(E), .Q(Q[0]), .Qn(Qn[0]), .reset(R));  // open: preset
  D_Flip_Flop d_ff_2 (.D(D[1]), .clk(E), .Q(Q[1]), .Qn(Qn[1]), .reset(R));  // open: preset
  D_Flip_Flop d_ff_3 (.D(D[2]), .clk(E), .Q(Q[2]), .Qn(Qn[2]), .reset(R));  // open: preset
  D_Flip_Flop d_ff_4 (.D(D[3]), .clk(E), .Q(Q[3]), .Qn(Qn[3]), .reset(R));  // open: preset
endmodule

module MAR_4b (
  input  [3:0] D,
  input  Clock,
  input  E,
  input  R,
  output [3:0] Q,
  output [3:0] Qn
);

  wire and_1_out, and_2_out, and_3_out, and_4_out;

  and and_1 (and_1_out, Clock, E);
  and and_2 (and_2_out, Clock, E);
  and and_3 (and_3_out, Clock, E);
  and and_4 (and_4_out, Clock, E);
  D_Flip_Flop d_ff_1 (.D(D[3]), .clk(and_1_out), .Q(Q[3]), .Qn(Qn[3]), .reset(R));  // open: preset
  D_Flip_Flop d_ff_2 (.D(D[2]), .clk(and_2_out), .Q(Q[2]), .Qn(Qn[2]), .reset(R));  // open: preset
  D_Flip_Flop d_ff_3 (.D(D[1]), .clk(and_3_out), .Q(Q[1]), .Qn(Qn[1]), .reset(R));  // open: preset
  D_Flip_Flop d_ff_4 (.D(D[0]), .clk(and_4_out), .Q(Q[0]), .Qn(Qn[0]), .reset(R));  // open: preset
endmodule

module MBR_4b_Pure (
  input  [3:0] ERxTx,
  input  Wr,
  input  Rd,
  input  Clk,
  input  E,
  input  [3:0] D,
  output [3:0] SRxTx,
  output [3:0] SnRxTx,
  output [3:0] Q,
  output [3:0] Qn
);

  wire and_1_out, buffer_tristate_ah_1b_1_q, buffer_tristate_ah_1b_7_q, buffer_tristate_ah_1b_13_q,
       buffer_tristate_ah_1b_19_q, d_ff_1_q, d_ff_1_qn, d_ff_2_q, d_ff_2_qn, d_ff_3_q, d_ff_3_qn, d_ff_4_q,
       d_ff_4_qn, decoder_4op_1b_2x4_1_m0, decoder_4op_1b_2x4_1_m1, decoder_4op_1b_2x4_1_m2, or_1_out,
       or_2_out, or_3_out, or_4_out, or_5_out, or_6_out, or_7_out, or_8_out;
  wire [1:0] helper_4op_to_3op_1_tr;

  Decoder_4op_1b_2x4 decoder_4op_1b_2x4_1 (
    .op(helper_4op_to_3op_1_tr), .m0(decoder_4op_1b_2x4_1_m0), .m1(decoder_4op_1b_2x4_1_m1),
    .m2(decoder_4op_1b_2x4_1_m2));  // open: m3
  Helper_4op_to_3op helper_4op_to_3op_1 (.op({Rd, Wr}), .tr(helper_4op_to_3op_1_tr));
  and and_1 (and_1_out, Clk, E);
  or or_1 (or_1_out, decoder_4op_1b_2x4_1_m1, decoder_4op_1b_2x4_1_m0);
  Buffer_TriState_AH_1b buffer_tristate_ah_1b_1 (
    .A(ERxTx[0]), .Ctrl(decoder_4op_1b_2x4_1_m2), .Q(buffer_tristate_ah_1b_1_q));
  D_Flip_Flop d_ff_1 (
    .D(buffer_tristate_ah_1b_1_q), .clk(and_1_out), .Q(d_ff_1_q), .Qn(d_ff_1_qn));  // open: preset, reset
  Buffer_TriState_AH_1b buffer_tristate_ah_1b_2 (.A(D[0]), .Ctrl(or_1_out), .Q(buffer_tristate_ah_1b_1_q));
  Buffer_TriState_AH_1b buffer_tristate_ah_1b_3 (.A(d_ff_1_qn), .Ctrl(decoder_4op_1b_2x4_1_m1), .Q(SnRxTx[0]));
  Buffer_TriState_AH_1b buffer_tristate_ah_1b_4 (.A(d_ff_1_q), .Ctrl(decoder_4op_1b_2x4_1_m1), .Q(SRxTx[0]));
  Buffer_TriState_AH_1b buffer_tristate_ah_1b_5 (.A(d_ff_1_q), .Ctrl(or_2_out), .Q(Q[0]));
  Buffer_TriState_AH_1b buffer_tristate_ah_1b_6 (.A(d_ff_1_qn), .Ctrl(or_2_out), .Q(Qn[0]));
  or or_2 (or_2_out, decoder_4op_1b_2x4_1_m2, decoder_4op_1b_2x4_1_m0);
  or or_3 (or_3_out, decoder_4op_1b_2x4_1_m1, decoder_4op_1b_2x4_1_m0);
  Buffer_TriState_AH_1b buffer_tristate_ah_1b_7 (
    .A(ERxTx[1]), .Ctrl(decoder_4op_1b_2x4_1_m2), .Q(buffer_tristate_ah_1b_7_q));
  Buffer_TriState_AH_1b buffer_tristate_ah_1b_8 (.A(D[1]), .Ctrl(or_3_out), .Q(buffer_tristate_ah_1b_7_q));
  D_Flip_Flop d_ff_2 (
    .D(buffer_tristate_ah_1b_7_q), .clk(and_1_out), .Q(d_ff_2_q), .Qn(d_ff_2_qn));  // open: preset, reset
  Buffer_TriState_AH_1b buffer_tristate_ah_1b_9 (.A(d_ff_2_qn), .Ctrl(decoder_4op_1b_2x4_1_m1), .Q(SnRxTx[1]));
  Buffer_TriState_AH_1b buffer_tristate_ah_1b_10 (.A(d_ff_2_q), .Ctrl(decoder_4op_1b_2x4_1_m1), .Q(SRxTx[1]));
  Buffer_TriState_AH_1b buffer_tristate_ah_1b_11 (.A(d_ff_2_q), .Ctrl(or_4_out), .Q(Q[1]));
  Buffer_TriState_AH_1b buffer_tristate_ah_1b_12 (.A(d_ff_2_qn), .Ctrl(or_4_out), .Q(Qn[1]));
  or or_4 (or_4_out, decoder_4op_1b_2x4_1_m2, decoder_4op_1b_2x4_1_m0);
  or or_5 (or_5_out, decoder_4op_1b_2x4_1_m1, decoder_4op_1b_2x4_1_m0);
  Buffer_TriState_AH_1b buffer_tristate_ah_1b_13 (
    .A(ERxTx[2]), .Ctrl(decoder_4op_1b_2x4_1_m2), .Q(buffer_tristate_ah_1b_13_q));
  Buffer_TriState_AH_1b buffer_tristate_ah_1b_14 (.A(D[2]), .Ctrl(or_5_out), .Q(buffer_tristate_ah_1b_13_q));
  D_Flip_Flop d_ff_3 (
    .D(buffer_tristate_ah_1b_13_q), .clk(and_1_out), .Q(d_ff_3_q), .Qn(d_ff_3_qn));  // open: preset, reset
  Buffer_TriState_AH_1b buffer_tristate_ah_1b_15 (.A(d_ff_3_qn), .Ctrl(decoder_4op_1b_2x4_1_m1), .Q(SnRxTx[2]));
  Buffer_TriState_AH_1b buffer_tristate_ah_1b_16 (.A(d_ff_3_q), .Ctrl(decoder_4op_1b_2x4_1_m1), .Q(SRxTx[2]));
  Buffer_TriState_AH_1b buffer_tristate_ah_1b_17 (.A(d_ff_3_q), .Ctrl(or_6_out), .Q(Q[2]));
  Buffer_TriState_AH_1b buffer_tristate_ah_1b_18 (.A(d_ff_3_qn), .Ctrl(or_6_out), .Q(Qn[2]));
  or or_6 (or_6_out, decoder_4op_1b_2x4_1_m2, decoder_4op_1b_2x4_1_m0);
  or or_7 (or_7_out, decoder_4op_1b_2x4_1_m1, decoder_4op_1b_2x4_1_m0);
  Buffer_TriState_AH_1b buffer_tristate_ah_1b_19 (
    .A(ERxTx[3]), .Ctrl(decoder_4op_1b_2x4_1_m2), .Q(buffer_tristate_ah_1b_19_q));
  Buffer_TriState_AH_1b buffer_tristate_ah_1b_20 (.A(D[3]), .Ctrl(or_7_out), .Q(buffer_tristate_ah_1b_19_q));
  D_Flip_Flop d_ff_4 (
    .D(buffer_tristate_ah_1b_19_q), .clk(and_1_out), .Q(d_ff_4_q), .Qn(d_ff_4_qn));  // open: preset, reset
  Buffer_TriState_AH_1b buffer_tristate_ah_1b_21 (.A(d_ff_4_qn), .Ctrl(decoder_4op_1b_2x4_1_m1), .Q(SnRxTx[3]));
  Buffer_TriState_AH_1b buffer_tristate_ah_1b_22 (.A(d_ff_4_q), .Ctrl(decoder_4op_1b_2x4_1_m1), .Q(SRxTx[3]));
  Buffer_TriState_AH_1b buffer_tristate_ah_1b_23 (.A(d_ff_4_q), .Ctrl(or_8_out), .Q(Q[3]));
  Buffer_TriState_AH_1b buffer_tristate_ah_1b_24 (.A(d_ff_4_qn), .Ctrl(or_8_out), .Q(Qn[3]));
  or or_8 (or_8_out, decoder_4op_1b_2x4_1_m2, decoder_4op_1b_2x4_1_m0);
endmodule

module MBR_4b (
  input  [3:0] ERxTx,
  input  Wr,
  input  Rd,
  input  Clk,
  input  E,
  input  [3:0] D,
  output [3:0] SRxTx,
  output [3:0] SnRxTx,
  output [3:0] Q,
  output [3:0] Qn
);

  wire and_1_out, decoder_4op_1b_2x4_1_m0, decoder_4op_1b_2x4_1_m1, decoder_4op_1b_2x4_1_m2,
       handler_mbr_1_sm0, handler_mbr_1_sm1, handler_mbr_1_sm2, handler_mbr_2_sm0, handler_mbr_2_sm1,
       handler_mbr_2_sm2, handler_mbr_3_sm0, handler_mbr_3_sm1, handler_mbr_3_sm2, handler_mbr_4_sm0,
       handler_mbr_4_sm1, handler_mbr_4_sm2;
  wire [1:0] helper_4op_to_3op_1_tr;

  Decoder_4op_1b_2x4 decoder_4op_1b_2x4_1 (
    .op(helper_4op_to_3op_1_tr), .m0(decoder_4op_1b_2x4_1_m0), .m1(decoder_4op_1b_2x4_1_m1),
    .m2(decoder_4op_1b_2x4_1_m2));  // open: m3
  Helper_4op_to_3op helper_4op_to_3op_1 (.op({Rd, Wr}), .tr(helper_4op_to_3op_1_tr));
  and and_1 (and_1_out, Clk, E);
  Handler_MBR handler_mbr_1 (
    .D(D[0]), .ERxTx(ERxTx[0]), .m2(decoder_4op_1b_2x4_1_m2), .m0(decoder_4op_1b_2x4_1_m0),
    .m1(decoder_4op_1b_2x4_1_m1), .ClkE(and_1_out), .SnRxTx(SnRxTx[0]), .Qn(Qn[0]), .Q(Q[0]),
    .SRxTx(SRxTx[0]), .sm2(handler_mbr_1_sm2), .sm0(handler_mbr_1_sm0), .sm1(handler_mbr_1_sm1));
  Handler_MBR handler_mbr_2 (
    .D(D[1]), .ERxTx(ERxTx[1]), .m2(handler_mbr_1_sm2), .m0(handler_mbr_1_sm0), .m1(handler_mbr_1_sm1),
    .ClkE(and_1_out), .SnRxTx(SnRxTx[1]), .Qn(Qn[1]), .Q(Q[1]), .SRxTx(SRxTx[1]), .sm2(handler_mbr_2_sm2),
    .sm0(handler_mbr_2_sm0), .sm1(handler_mbr_2_sm1));
  Handler_MBR handler_mbr_3 (
    .D(D[2]), .ERxTx(ERxTx[2]), .m2(handler_mbr_2_sm2), .m0(handler_mbr_2_sm0), .m1(handler_mbr_2_sm1),
    .ClkE(and_1_out), .SnRxTx(SnRxTx[2]), .Qn(Qn[2]), .Q(Q[2]), .SRxTx(SRxTx[2]), .sm2(handler_mbr_3_sm2),
    .sm0(handler_mbr_3_sm0), .sm1(handler_mbr_3_sm1));
  Handler_MBR handler_mbr_4 (
    .D(D[3]), .ERxTx(ERxTx[3]), .m2(handler_mbr_3_sm2), .m0(handler_mbr_3_sm0), .m1(handler_mbr_3_sm1),
    .ClkE(and_1_out), .SnRxTx(SnRxTx[3]), .Qn(Qn[3]), .Q(Q[3]), .SRxTx(SRxTx[3]), .sm2(handler_mbr_4_sm2),
    .sm0(handler_mbr_4_sm0), .sm1(handler_mbr_4_sm1));
endmodule

module Handler_MBR (
  input  ERxTx,
  input  m0,
  input  m1,
  input  m2,
  input  ClkE,
  input  D,
  output SnRxTx,
  output SRxTx,
  output sm0,
  output sm1,
  output sm2,
  output Qn,
  output Q
);

  wire buffer_tristate_ah_1b_1_q, d_ff_1_q, d_ff_1_qn, or_1_out, or_2_out;

  or or_1 (or_1_out, m1, m0);
  Buffer_TriState_AH_1b buffer_tristate_ah_1b_1 (.A(ERxTx), .Ctrl(m2), .Q(buffer_tristate_ah_1b_1_q));
  D_Flip_Flop d_ff_1 (.D(buffer_tristate_ah_1b_1_q), .clk(ClkE), .Q(d_ff_1_q), .Qn(d_ff_1_qn));  // open: preset, reset
  Buffer_TriState_AH_1b buffer_tristate_ah_1b_2 (.A(D), .Ctrl(or_1_out), .Q(buffer_tristate_ah_1b_1_q));
  Buffer_TriState_AH_1b buffer_tristate_ah_1b_3 (.A(d_ff_1_qn), .Ctrl(m1), .Q(SnRxTx));
  Buffer_TriState_AH_1b buffer_tristate_ah_1b_4 (.A(d_ff_1_qn), .Ctrl(or_2_out), .Q(Qn));
  Buffer_TriState_AH_1b buffer_tristate_ah_1b_5 (.A(d_ff_1_q), .Ctrl(m1), .Q(SRxTx));
  or or_2 (or_2_out, m2, m0);
  Buffer_TriState_AH_1b buffer_tristate_ah_1b_6 (.A(d_ff_1_q), .Ctrl(or_2_out), .Q(Q));

  assign sm0 = m0;
  assign sm1 = m1;
  assign sm2 = m2;
endmodule

module Register_4b (
  input  [3:0] C,
  input  ClkE,
  input  EA,
  input  EB,
  output [3:0] A,
  output [3:0] B
);

  wire d_ff_1_q, d_ff_2_q, d_ff_3_q, d_ff_4_q, handler_register_1_eas, handler_register_1_ebs,
       handler_register_2_eas, handler_register_2_ebs, handler_register_3_eas, handler_register_3_ebs,
       handler_register_4_eas, handler_register_4_ebs;

  D_Flip_Flop d_ff_1 (.D(C[0]), .clk(ClkE), .Q(d_ff_1_q));  // open: Qn, preset, reset
  D_Flip_Flop d_ff_2 (.D(C[1]), .clk(ClkE), .Q(d_ff_2_q));  // open: Qn, preset, reset
  D_Flip_Flop d_ff_3 (.D(C[2]), .clk(ClkE), .Q(d_ff_3_q));  // open: Qn, preset, reset
  D_Flip_Flop d_ff_4 (.D(C[3]), .clk(ClkE), .Q(d_ff_4_q));  // open: Qn, preset, reset
  Handler_Register handler_register_1 (
    .EB(EB), .c(d_ff_1_q), .EA(EA), .EBs(handler_register_1_ebs), .b(B[0]), .a(A[0]),
    .EAs(handler_register_1_eas));
  Handler_Register handler_register_2 (
    .EB(handler_register_1_ebs), .c(d_ff_2_q), .EA(handler_register_1_eas), .EBs(handler_register_2_ebs),
    .b(B[1]), .a(A[1]), .EAs(handler_register_2_eas));
  Handler_Register handler_register_3 (
    .EB(handler_register_2_ebs), .c(d_ff_3_q), .EA(handler_register_2_eas), .EBs(handler_register_3_ebs),
    .b(B[2]), .a(A[2]), .EAs(handler_register_3_eas));
  Handler_Register handler_register_4 (
    .EB(handler_register_3_ebs), .c(d_ff_4_q), .EA(handler_register_3_eas), .EBs(handler_register_4_ebs),
    .b(B[3]), .a(A[3]), .EAs(handler_register_4_eas));
  // Probe on A
  // Probe on B
endmodule

module Handler_Register (
  input  EA,
  input  EB,
  input  c,
  output a,
  output b,
  output EAs,
  output EBs
);

  Buffer_TriState_AH_1b buffer_tristate_ah_1b_1 (.A(c), .Ctrl(EA), .Q(a));
  Buffer_TriState_AH_1b buffer_tristate_ah_1b_2 (.A(c), .Ctrl(EB), .Q(b));

  assign EAs = EA;
  assign EBs = EB;
endmodule

module Register_Bank_4b (
  input  C2,
  input  C1,
  input  C0,
  input  A2,
  input  A1,
  input  A0,
  input  B2,
  input  B1,
  input  B0,
  input  Clk,
  input  E,
  input  [3:0] D,
  output [3:0] A,
  output [3:0] B
);

  wire and_1_out, and_2_out, and_3_out, and_4_out, and_5_out, and_6_out, and_7_out, and_8_out, and_9_out,
       decoder_8op_3x8_1_m0, decoder_8op_3x8_1_m1, decoder_8op_3x8_1_m2, decoder_8op_3x8_1_m3,
       decoder_8op_3x8_1_m4, decoder_8op_3x8_1_m5, decoder_8op_3x8_1_m6, decoder_8op_3x8_1_m7,
       decoder_8op_3x8_2_m0, decoder_8op_3x8_2_m1, decoder_8op_3x8_2_m2, decoder_8op_3x8_2_m3,
       decoder_8op_3x8_2_m4, decoder_8op_3x8_2_m5, decoder_8op_3x8_2_m6, decoder_8op_3x8_2_m7,
       decoder_8op_3x8_3_m0, decoder_8op_3x8_3_m1, decoder_8op_3x8_3_m2, decoder_8op_3x8_3_m3,
       decoder_8op_3x8_3_m4, decoder_8op_3x8_3_m5, decoder_8op_3x8_3_m6, decoder_8op_3x8_3_m7;

  Decoder_8op_3x8 decoder_8op_3x8_1 (
    .op({C2, C1, C0}), .m0(decoder_8op_3x8_1_m0), .m1(decoder_8op_3x8_1_m1), .m2(decoder_8op_3x8_1_m2),
    .m3(decoder_8op_3x8_1_m3), .m4(decoder_8op_3x8_1_m4), .m5(decoder_8op_3x8_1_m5),
    .m6(decoder_8op_3x8_1_m6), .m7(decoder_8op_3x8_1_m7));
  and and_1 (and_1_out, Clk, E);
  and and_2 (and_2_out, decoder_8op_3x8_1_m0, and_1_out);
  and and_3 (and_3_out, decoder_8op_3x8_1_m1, and_1_out);
  and and_4 (and_4_out, decoder_8op_3x8_1_m2, and_1_out);
  and and_5 (and_5_out, decoder_8op_3x8_1_m3, and_1_out);
  and and_6 (and_6_out, decoder_8op_3x8_1_m4, and_1_out);
  and and_7 (and_7_out, decoder_8op_3x8_1_m5, and_1_out);
  and and_8 (and_8_out, decoder_8op_3x8_1_m6, and_1_out);
  and and_9 (and_9_out, decoder_8op_3x8_1_m7, and_1_out);
  Register_4b R0 (.C(D), .ClkE(and_2_out), .EA(decoder_8op_3x8_2_m0), .EB(decoder_8op_3x8_3_m0), .A(A), .B(B));
  Register_4b R1 (.C(D), .ClkE(and_3_out), .EA(decoder_8op_3x8_2_m1), .EB(decoder_8op_3x8_3_m1), .A(A), .B(B));
  Register_4b R2 (.C(D), .ClkE(and_4_out), .EA(decoder_8op_3x8_2_m2), .EB(decoder_8op_3x8_3_m2), .A(A), .B(B));
  Register_4b R3 (.C(D), .ClkE(and_5_out), .EA(decoder_8op_3x8_2_m3), .EB(decoder_8op_3x8_3_m3), .A(A), .B(B));
  Register_4b R4 (.C(D), .ClkE(and_6_out), .EA(decoder_8op_3x8_2_m4), .EB(decoder_8op_3x8_3_m4), .A(A), .B(B));
  Register_4b R5 (.C(D), .ClkE(and_7_out), .EA(decoder_8op_3x8_2_m5), .EB(decoder_8op_3x8_3_m5), .A(A), .B(B));
  Register_4b R6 (.C(D), .ClkE(and_8_out), .EA(decoder_8op_3x8_2_m6), .EB(decoder_8op_3x8_3_m6), .A(A), .B(B));
  Register_4b R7 (.C(D), .ClkE(and_9_out), .EA(decoder_8op_3x8_2_m7), .EB(decoder_8op_3x8_3_m7), .A(A), .B(B));
  Decoder_8op_3x8 decoder_8op_3x8_2 (
    .op({A2, A1, A0}), .m0(decoder_8op_3x8_2_m0), .m1(decoder_8op_3x8_2_m1), .m2(decoder_8op_3x8_2_m2),
    .m3(decoder_8op_3x8_2_m3), .m4(decoder_8op_3x8_2_m4), .m5(decoder_8op_3x8_2_m5),
    .m6(decoder_8op_3x8_2_m6), .m7(decoder_8op_3x8_2_m7));
  // Probe on A
  // Probe on A
  Decoder_8op_3x8 decoder_8op_3x8_3 (
    .op({B2, B1, B0}), .m0(decoder_8op_3x8_3_m0), .m1(decoder_8op_3x8_3_m1), .m2(decoder_8op_3x8_3_m2),
    .m3(decoder_8op_3x8_3_m3), .m4(decoder_8op_3x8_3_m4), .m5(decoder_8op_3x8_3_m5),
    .m6(decoder_8op_3x8_3_m6), .m7(decoder_8op_3x8_3_m7));
  // Probe on B
  // Probe on B
endmodule
