// Logisim project G9_TriState_Buffers_Inverters.circ as structural Verilog: 13 circuits, main circuit Buffer_TriState_AH_1b
module Transmission_Gate (
  input  A,
  input  P_Gate,
  input  N_Gate,
  output Q
);

  Transistor transistor_1 (.in(A), .out(Q), .gate(P_Gate));
  Transistor #(.\type ("n")) transistor_2 (.in(A), .out(Q), .gate(N_Gate));
endmodule

module Buffer_TriState_AH_1b (
  input  Ctrl,
  input  A,
  output Q
);

  wire not_1_out, not_2_out;

  not not_1 (not_1_out, Ctrl);
  Transmission_Gate transmission_gate_1 (.A(A), .N_Gate(not_2_out), .P_Gate(not_1_out), .Q(Q));
  not not_2 (not_2_out, not_1_out);

  // Notes on the sheet:
  //   Tri-State Buffer (Active High Enable)
  //   Ctrl | A | Q (tristate real)
  //   0 | 0 | Z (Hi-Z)
  //   0 | 1 | Z (Hi-Z)
  //   1 | 0 | 0
  //   1 | 1 | 1
endmodule

module Buffer_TriState_AL_1b (
  input  Ctrl_N,
  input  A,
  output Q
);

  wire not_1_out;

  Transmission_Gate transmission_gate_1 (.A(A), .N_Gate(not_1_out), .P_Gate(Ctrl_N), .Q(Q));
  not not_1 (not_1_out, Ctrl_N);

  // Notes on the sheet:
  //   Tri-State Buffer (Active Low Enable)
  //   Ctrl | A | Q
  //   0 | 0 | 0
  //   0 | 1 | 1
  //   1 | 0 | Z (Hi-Z)
  //   1 | 1 | Z (Hi-Z)
endmodule

module Inverter_TriState_AH_1b (
  input  Ctrl,
  input  A,
  output Q
);

  wire not_1_out, not_2_out, not_3_out;

  not not_1 (not_1_out, Ctrl);
  not not_2 (not_2_out, A);
  not not_3 (not_3_out, not_1_out);
  Transmission_Gate transmission_gate_1 (.A(not_2_out), .N_Gate(not_3_out), .P_Gate(not_1_out), .Q(Q));

  // Notes on the sheet:
  //   Tri-State Inverter (Active High Enable)
  //   Ctrl | A | Q
  //   0 | 0 | Z (Hi-Z)
  //   0 | 1 | Z (Hi-Z)
  //   1 | 0 | 1
  //   1 | 1 | 0
endmodule

module Inverter_TriState_AL_1b (
  input  Ctrl,
  input  A,
  output Q
);

  wire not_1_out, not_2_out;

  not not_1 (not_1_out, A);
  not not_2 (not_2_out, Ctrl);
  Transmission_Gate transmission_gate_1 (.A(not_1_out), .N_Gate(not_2_out), .P_Gate(Ctrl), .Q(Q));

  // Notes on the sheet:
  //   Tri-State Inverter (Active Low Enable)
  //   Ctrl | A | Q
  //   0 | 0 | 1
  //   0 | 1 | 0
  //   1 | 0 | Z (Hi-Z)
  //   1 | 1 | Z (Hi-Z)
endmodule

module Buffer_TriState_AH_2b (
  input  Ctrl,
  input  [1:0] A,
  output [1:0] Q
);

  Buffer_TriState_AH_1b buffer_tristate_ah_1b_1 (.A(A[0]), .Ctrl(Ctrl), .Q(Q[0]));
  Buffer_TriState_AH_1b buffer_tristate_ah_1b_2 (.A(A[1]), .Ctrl(Ctrl), .Q(Q[1]));
endmodule

module Buffer_TriState_AL_2b (
  input  Ctrl,
  input  [1:0] A,
  output [1:0] Q
);

  Buffer_TriState_AL_1b buffer_tristate_al_1b_1 (.A(A[0]), .Ctrl_N(Ctrl), .Q(Q[0]));
  Buffer_TriState_AL_1b buffer_tristate_al_1b_2 (.A(A[1]), .Ctrl_N(Ctrl), .Q(Q[1]));
endmodule

module Inverter_TriState_AH_2b (
  input  Ctrl,
  input  [1:0] A,
  output [1:0] Q
);

  Inverter_TriState_AH_1b inverter_tristate_ah_1b_1 (.Ctrl(Ctrl), .A(A[0]), .Q(Q[0]));
  Inverter_TriState_AH_1b inverter_tristate_ah_1b_2 (.Ctrl(Ctrl), .A(A[1]), .Q(Q[1]));
endmodule

module Inverter_TriState_AL_2b (
  input  Ctrl,
  input  [1:0] A,
  output [1:0] Q
);

  Inverter_TriState_AL_1b inverter_tristate_al_1b_1 (.Ctrl(Ctrl), .A(A[0]), .Q(Q[0]));
  Inverter_TriState_AL_1b inverter_tristate_al_1b_2 (.Ctrl(Ctrl), .A(A[1]), .Q(Q[1]));
endmodule

module Buffer_TriState_AH_4b (
  input  Ctrl,
  input  [3:0] A,
  output [3:0] Q
);

  Buffer_TriState_AH_1b buffer_tristate_ah_1b_1 (.A(A[0]), .Ctrl(Ctrl), .Q(Q[0]));
  Buffer_TriState_AH_1b buffer_tristate_ah_1b_2 (.A(A[1]), .Ctrl(Ctrl), .Q(Q[1]));
  Buffer_TriState_AH_1b buffer_tristate_ah_1b_3 (.A(A[2]), .Ctrl(Ctrl), .Q(Q[2]));
  Buffer_TriState_AH_1b buffer_tristate_ah_1b_4 (.A(A[3]), .Ctrl(Ctrl), .Q(Q[3]));
endmodule

module Buffer_TriState_AL_4b (
  input  Ctrl,
  input  [3:0] A,
  output [3:0] Q
);

  Buffer_TriState_AL_1b buffer_tristate_al_1b_1 (.A(A[0]), .Ctrl_N(Ctrl), .Q(Q[0]));
  Buffer_TriState_AL_1b buffer_tristate_al_1b_2 (.A(A[1]), .Ctrl_N(Ctrl), .Q(Q[1]));
  Buffer_TriState_AL_1b buffer_tristate_al_1b_3 (.A(A[2]), .Ctrl_N(Ctrl), .Q(Q[2]));
  Buffer_TriState_AL_1b buffer_tristate_al_1b_4 (.A(A[3]), .Ctrl_N(Ctrl), .Q(Q[3]));
endmodule

module Inverter_TriState_AH_4b (
  input  Ctrl,
  input  [3:0] A,
  output [3:0] Q
);

  Inverter_TriState_AH_1b inverter_tristate_ah_1b_1 (.Ctrl(Ctrl), .A(A[0]), .Q(Q[0]));
  Inverter_TriState_AH_1b inverter_tristate_ah_1b_2 (.Ctrl(Ctrl), .A(A[1]), .Q(Q[1]));
  Inverter_TriState_AH_1b inverter_tristate_ah_1b_3 (.Ctrl(Ctrl), .A(A[2]), .Q(Q[2]));
  Inverter_TriState_AH_1b inverter_tristate_ah_1b_4 (.Ctrl(Ctrl), .A(A[3]), .Q(Q[3]));
endmodule

module Inverter_TriState_AL_4b (
  input  Ctrl,
  input  [3:0] A,
  output [3:0] Q
);

  Inverter_TriState_AL_1b inverter_tristate_al_1b_1 (.Ctrl(Ctrl), .A(A[0]), .Q(Q[0]));
  Inverter_TriState_AL_1b inverter_tristate_al_1b_2 (.Ctrl(Ctrl), .A(A[1]), .Q(Q[1]));
  Inverter_TriState_AL_1b inverter_tristate_al_1b_3 (.Ctrl(Ctrl), .A(A[2]), .Q(Q[2]));
  Inverter_TriState_AL_1b inverter_tristate_al_1b_4 (.Ctrl(Ctrl), .A(A[3]), .Q(Q[3]));
endmodule
