// Logisim project _ULACOMTRATAMENTO.circ as structural Verilog: 12 circuits, main circuit DEMO_ula_4b
module DEMO_ula_4b (
  input  [3:0] InputA,
  input  [3:0] InputB,
  input  [1:0] Op,
  output [3:0] Saida
);

  Hex_Digit_Display hex_digit_display_1 (.value(InputA));  // open: dp
  ula_4b ula_4b_1 (.Op(Op), .BusA(InputA), .BusB(InputB), .BusS(Saida));  // open: out_5, out_6
  Hex_Digit_Display hex_digit_display_2 (.value(InputB));  // open: dp
  Hex_Digit_Display hex_digit_display_3 (.value(Saida));  // open: dp

  // Notes on the sheet:
  //   00 : Adder ( + )
  //   01 : Buffer ( # )
  //   10 : Nand ( !& )
  //   11 : Subtractor ( - )
endmodule

module ula_4b (
  input  [3:0] BusA,
  input  [3:0] BusB,
  input  [1:0] Op,
  output [3:0] BusS,
  output out_5,
  output out_6
);

  wire and_1_out, and_2_out, Bo, Co, nand_1_out, nor_1_out, nor_2_out, nor_3_out;
  wire [3:0] adder_4b_1_s_ad4b, buffer_4b_1_s, nand_4b_1_s, subtractor_4b_1_s;

  Hex_Digit_Display hex_digit_display_1 (.value(BusA));  // open: dp
  Hex_Digit_Display hex_digit_display_2 (.value(BusB));  // open: dp
  _7_Segment_Display u_7_segment_display_1 (.a(out_5));  // open: g, f, b, e, d, c, dp
  _7_Segment_Display u_7_segment_display_2 (.g(out_6));  // open: f, a, b, e, d, c, dp
  Hex_Digit_Display hex_digit_display_3 (.value(BusS));  // open: dp
  nand nand_1 (nand_1_out, Op[0], Op[1]);
  and and_1 (and_1_out, Op[0], Op[1]);
  Adder_4b adder_4b_1 (.A(BusA), .B(BusB), .Co_Ad4b(Co), .S_Ad4b(adder_4b_1_s_ad4b));  // open: Ci_Ad4b
  Buffer_4b buffer_4b_1 (.A(BusA), .S(buffer_4b_1_s));
  Nand_4b nand_4b_1 (.A(BusA), .B(BusB), .S(nand_4b_1_s));
  Subtractor_4b subtractor_4b_1 (.A(BusA), .B(BusB), .Bo(Bo), .S(subtractor_4b_1_s));
  and and_2 (and_2_out, and_1_out, nor_3_out);
  nor nor_1 (nor_1_out, BusA[0], BusA[1], BusA[2], BusA[3]);
  nor nor_2 (nor_2_out, BusB[0], BusB[1], BusB[2], BusB[3]);
  and and_3 (out_5, Co, nand_1_out);
  nor nor_3 (nor_3_out, nor_1_out, nor_2_out);
  Multiplexador_4op_4b multiplexador_4op_4b_1 (
    .A(adder_4b_1_s_ad4b), .B(buffer_4b_1_s), .C(nand_4b_1_s), .D(subtractor_4b_1_s), .Op(Op), .S(BusS));
  and and_4 (out_6, Bo, and_2_out);

  // Other names for the same wires on the sheet: Adder_Si = out_5; Subt_Si = out_6

  // Notes on the sheet:
  //   00 : Adder ( + )
  //   01 : Buffer ( # )
  //   10 : Nand ( !& )
  //   11 : Subtractor ( - )
endmodule

module Adder_Half (
  input  A,
  input  B,
  output S_Adh,
  output Co_Adh
);

  xor xor_1 (S_Adh, A, B);
  and and_1 (Co_Adh, A, B);

  // Notes on the sheet:
  //   S_Adh = A ⊕ B
  //   Co_Adh = A . B
endmodule

module Adder_1b (
  input  A,
  input  B,
  input  Ci,
  output S_Ad1b,
  output Co_Ad1b
);

  wire adder_half_1_co_adh, adder_half_1_s_adh, adder_half_2_co_adh;

  Adder_Half adder_half_1 (.B(B), .A(A), .Co_Adh(adder_half_1_co_adh), .S_Adh(adder_half_1_s_adh));
  Adder_Half adder_half_2 (.B(Ci), .A(adder_half_1_s_adh), .Co_Adh(adder_half_2_co_adh), .S_Adh(S_Ad1b));
  or or_1 (Co_Ad1b, adder_half_2_co_adh, adder_half_1_co_adh);

  // Notes on the sheet:
  //   S_Ad1b = A ⊕ B ⊕ Ci_n​i
  //   Co_Ad1b ​= (A.B) + ( Ci_in​ . (A⊕B) )
  //   T1 = A ⊕ B
  //   T2 = A.B
  //   T3 = Ci_in . T1
  //   S_Ad1b = T1 ⊕ Ci_in​
  //   Co_Ad1b ​= T2 + T3
endmodule

module Adder_4b (
  input  [3:0] A,
  input  [3:0] B,
  input  Ci_Ad4b,
  output [3:0] S_Ad4b,
  output Co_Ad4b
);

  wire adder_1b_1_co_ad1b, adder_1b_2_co_ad1b, adder_1b_3_co_ad1b;

  Adder_1b adder_1b_1 (.Ci(Ci_Ad4b), .A(A[0]), .B(B[0]), .Co_Ad1b(adder_1b_1_co_ad1b), .S_Ad1b(S_Ad4b[0]));
  Adder_1b adder_1b_2 (.Ci(adder_1b_1_co_ad1b), .A(A[1]), .B(B[1]), .Co_Ad1b(adder_1b_2_co_ad1b), .S_Ad1b(S_Ad4b[1]));
  Adder_1b adder_1b_3 (.Ci(adder_1b_2_co_ad1b), .A(A[2]), .B(B[2]), .Co_Ad1b(adder_1b_3_co_ad1b), .S_Ad1b(S_Ad4b[2]));
  Adder_1b adder_1b_4 (.Ci(adder_1b_3_co_ad1b), .A(A[3]), .B(B[3]), .Co_Ad1b(Co_Ad4b), .S_Ad1b(S_Ad4b[3]));

  // Notes on the sheet:
  //   metodo:
  //   ripple-carry
endmodule

module Buffer_4b (
  input  [3:0] A,
  output [3:0] S
);

  buf buffer_1 (S[3], A[3]);
  buf buffer_2 (S[2], A[2]);
  buf buffer_3 (S[1], A[1]);
  buf buffer_4 (S[0], A[0]);
endmodule

module Nand_4b (
  input  [3:0] A,
  input  [3:0] B,
  output [3:0] S
);

  nand nand_1 (S[0], B[0], A[0]);
  nand nand_2 (S[1], B[1], A[1]);
  nand nand_3 (S[2], B[2], A[1]);
  nand nand_4 (S[3], B[3], A[2]);
endmodule

module Subtractor_4b (
  input  [3:0] A,
  input  [3:0] B,
  output [3:0] S,
  output Bo
);

  wire [3:0] nand_4b_1_s;

  Nand_4b nand_4b_1 (.A(B), .B(B), .S(nand_4b_1_s));
  Adder_4b adder_4b_1 (.A(A), .B(nand_4b_1_s), .Ci_Ad4b(1'b1), .Co_Ad4b(Bo), .S_Ad4b(S));
endmodule

module Decoder_4op_1b (
  input  o0,
  input  o1,
  output m0,
  output m1,
  output m2,
  output m3
);

  wire buffer_1_out, buffer_2_out, not_1_out, not_2_out;

  buf buffer_1 (buffer_1_out, o1);
  buf buffer_2 (buffer_2_out, o0);
  not not_1 (not_1_out, o1);
  not not_2 (not_2_out, o0);
  and and_1 (m0, not_2_out, not_1_out);
  and and_2 (m1, not_1_out, buffer_2_out);
  and and_3 (m2, not_2_out, buffer_1_out);
  and and_4 (m3, buffer_2_out, buffer_1_out);
endmodule

module Multiplexador_4op_1b (
  input  i0,
  input  i1,
  input  i2,
  input  i3,
  input  Op0,
  input  Op1,
  output out_7
);

  wire and_1_out, and_2_out, and_3_out, and_4_out, decoder_4op_1b_1_m0, decoder_4op_1b_1_m1,
       decoder_4op_1b_1_m2, decoder_4op_1b_1_m3;

  Decoder_4op_1b decoder_4op_1b_1 (
    .o0(Op0), .o1(Op1), .m0(decoder_4op_1b_1_m0), .m1(decoder_4op_1b_1_m1), .m2(decoder_4op_1b_1_m2),
    .m3(decoder_4op_1b_1_m3));
  and and_1 (and_1_out, decoder_4op_1b_1_m3, i3);
  and and_2 (and_2_out, decoder_4op_1b_1_m2, i2);
  and and_3 (and_3_out, decoder_4op_1b_1_m1, i1);
  and and_4 (and_4_out, decoder_4op_1b_1_m0, i0);
  or or_1 (out_7, and_1_out, and_2_out, and_3_out, and_4_out);
endmodule

module Multiplexador_4op_4b (
  input  [3:0] A,
  input  [3:0] B,
  input  [3:0] C,
  input  [3:0] D,
  input  [1:0] Op,
  output [3:0] S
);

  Multiplexador_4op_1b multiplexador_4op_1b_1 (
    .Op0(Op[0]), .Op1(Op[1]), .i3(D[0]), .i0(A[0]), .i1(B[0]), .i2(C[0]), .out_7(S[0]));
  Multiplexador_4op_1b multiplexador_4op_1b_2 (
    .Op0(Op[0]), .Op1(Op[1]), .i3(D[1]), .i0(A[1]), .i1(B[1]), .i2(C[1]), .out_7(S[1]));
  Multiplexador_4op_1b multiplexador_4op_1b_3 (
    .Op0(Op[0]), .Op1(Op[1]), .i3(D[2]), .i0(A[2]), .i1(B[2]), .i2(C[2]), .out_7(S[2]));
  Multiplexador_4op_1b multiplexador_4op_1b_4 (
    .Op0(Op[0]), .Op1(Op[1]), .i3(D[3]), .i0(A[3]), .i1(B[3]), .i2(C[3]), .out_7(S[3]));
endmodule

module PrintMacros (
);

  ula_4b ula_4b_1 ();  // open: Op, BusA, BusB, BusS, out_5, out_6
endmodule
