// Logisim project G9_ALU_8op4b.circ as structural Verilog: 7 circuits, main circuit ALU_4b8op
module ALU_4b8op (
  input  [3:0] A,
  input  [3:0] B,
  input  [2:0] op,
  output [3:0] Q
);

  wire [3:0] adder_4b_1_q, divider_4b_1_q, multiplier_4b_1_q, nand_1_out, nor_1_out, subtractor_4b_1_q,
       xnor_1_out, xor_1_out;

  Adder_4b adder_4b_1 (.A(A), .B(B), .Q(adder_4b_1_q));  // open: Ci, Co
  Divider_4b divider_4b_1 (.B(B), .A(A), .Q(divider_4b_1_q));  // open: Upper, Rems
  Multiplier_4b multiplier_4b_1 (.B(B), .A(A), .Q(multiplier_4b_1_q));  // open: Ci, Co
  assign nand_1_out = ~(A & B);  // NAND_Gate nand_1, 4 bits wide
  assign nor_1_out = ~(A | B);  // NOR_Gate nor_1, 4 bits wide
  Subtractor_4b subtractor_4b_1 (.B(B), .A(A), .Q(subtractor_4b_1_q));  // open: Bo
  assign xor_1_out = A ^ B;  // XOR_Gate xor_1, 4 bits wide
  assign xnor_1_out = ~(A ^ B);  // XNOR_Gate xnor_1, 4 bits wide
  Multiplexador_8op_4b multiplexador_8op_4b_1 (
    .E(nor_1_out), .B(divider_4b_1_q), .F(subtractor_4b_1_q), .C(multiplier_4b_1_q), .G(xnor_1_out),
    .D(nand_1_out), .H(xor_1_out), .op(op), .A(adder_4b_1_q), .Q(Q));
endmodule

module Adder_Half (
  input  A,
  input  B,
  output Q,
  output Co
);

  xor xor_1 (Q, A, B);
  and and_1 (Co, A, B);

  // Notes on the sheet:
  //   Q = A ⊕ B
  //   Co = A • B
endmodule

module Adder_Full_1b (
  input  A,
  input  B,
  input  Ci,
  output Co,
  output Q
);

  wire adder_half_1_co, adder_half_1_q, adder_half_2_co;

  Adder_Half adder_half_1 (.A(A), .B(B), .Q(adder_half_1_q), .Co(adder_half_1_co));
  Adder_Half adder_half_2 (.A(adder_half_1_q), .B(Ci), .Q(Q), .Co(adder_half_2_co));
  or or_1 (Co, adder_half_2_co, adder_half_1_co);

  // Notes on the sheet:
  //   Q = A ⊕ B ⊕ Ci
  //   Co ​= ( A • B ) + ( Ci_in​ • ( A ⊕ B ) )
  //   T1 = A ⊕ B
  //   T2 = A • B
  //   T3 = Ci • T1
  //   Q = T1 ⊕ Ci
  //   Co ​= T2 + T3
endmodule

module Adder_4b (
  input  [3:0] A,
  input  [3:0] B,
  input  Ci,
  output Co,
  output [3:0] Q
);

  wire adder_full_1b_1_co, adder_full_1b_2_co, adder_full_1b_3_co;

  Adder_Full_1b adder_full_1b_1 (.Ci(Ci), .A(A[0]), .B(B[0]), .Co(adder_full_1b_1_co), .Q(Q[0]));
  Adder_Full_1b adder_full_1b_2 (.Ci(adder_full_1b_1_co), .A(A[1]), .B(B[1]), .Co(adder_full_1b_2_co), .Q(Q[1]));
  Adder_Full_1b adder_full_1b_3 (.Ci(adder_full_1b_2_co), .A(A[2]), .B(B[2]), .Co(adder_full_1b_3_co), .Q(Q[2]));
  Adder_Full_1b adder_full_1b_4 (.Ci(adder_full_1b_3_co), .A(A[3]), .B(B[3]), .Co(Co), .Q(Q[3]));
endmodule

module Subtractor_4b (
  input  [3:0] A,
  input  [3:0] B,
  output [3:0] Q,
  output Bo
);

  wire [3:0] nand_1_out;

  assign nand_1_out = ~(B & B);  // NAND_Gate nand_1, 4 bits wide
  Adder_4b adder_4b_1 (.A(A), .B(nand_1_out), .Ci(1'b1), .Co(Bo), .Q(Q));
endmodule

module Multiplier_4b (
  input  [3:0] Ci,
  input  [3:0] A,
  input  [3:0] B,
  output [3:0] Q,
  output [3:0] Co
);

  Multiplier #(.width(4)) multiplier_1 (.a(A), .b(B), .out(Q), .cin(Ci), .cout(Co));
endmodule

module Divider_4b (
  input  [3:0] Upper,
  input  [3:0] A,
  input  [3:0] B,
  output [3:0] Q,
  output [3:0] Rems
);

  Divider #(.width(4)) divider_1 (.a(A), .b(B), .out(Q), .upper(Upper), .rem(Rems));
endmodule
