// Logisim project G9_CPU.circ as structural Verilog: 1 circuit, main circuit CPU
module CPU (
  input  E4,
  input  E3,
  input  E2,
  input  E1,
  input  E0,
  input  T3,
  input  T2,
  input  T1,
  input  T0
);

  wire CLK_LATCH_out, CLK_MAR_out, CLK_MBR_REGISTERS_out, CLK_MIR_out, mir_1_a19, mir_1_q0, mir_1_q1,
       mir_1_q2, mir_1_q3, mir_1_q4, mir_1_q5, mir_1_q6, mir_1_q7, mir_1_q8, mir_1_q9, mir_1_q10, mir_1_q11,
       mir_1_q12, mir_1_q13, mir_bank_1_q0, mir_bank_1_q1, mir_bank_1_q2, mir_bank_1_q3, mir_bank_1_q4,
       mir_bank_1_q5, mir_bank_1_q6, mir_bank_1_q7, mir_bank_1_q8, mir_bank_1_q9, mir_bank_1_q10,
       mir_bank_1_q11, mir_bank_1_q12, mir_bank_1_q13, mir_bank_1_q14, mir_bank_1_q15, mir_bank_1_q16,
       mir_bank_1_q17, mir_bank_1_q18, mir_bank_1_q19, mir_bank_1_q20, mir_bank_1_q21, mir_bank_1_q22,
       mir_bank_1_q23;
  wire [1:0] mir_1_q14;
  wire [2:0] mir_1_q16;
  wire [3:0] a_multiplexador_2op_4b_1_q, alu_4b8op_1_q, latch_master_4b_1_q, latch_master_4b_2_q, mar_4b_1_a,
       mbr_4b_1_s, mbr_4b_1_sexit, register_bank_4b_1_a, register_bank_4b_1_b, rxtx_transceiver_1_dis,
       rxtx_transceiver_1_sext, shifter_3op_4b_1_q;

  Hex_Digit_Display hex_digit_display_1 (.value(rxtx_transceiver_1_dis));  // open: dp
  RxTx_Transceiver rxtx_transceiver_1 (
    .T_R(mar_4b_1_a[0]), .BusExt(mbr_4b_1_sexit), .TEC({T3, T2, T1, T0}), .DIS(rxtx_transceiver_1_dis),
    .SExt(rxtx_transceiver_1_sext));
  MAR_4b mar_4b_1 (.D(latch_master_4b_2_q), .Clock(CLK_MAR_out), .E(mir_1_q13), .A(mar_4b_1_a));  // open: R, An
  Clock #(.lowDuration(3), .phaseOffset(3)) CLK_MBR_REGISTERS (.out(CLK_MBR_REGISTERS_out));
  Clock #(.lowDuration(3), .phaseOffset(2)) CLK_MAR (.out(CLK_MAR_out));
  Clock #(.lowDuration(3), .phaseOffset(1)) CLK_LATCH (.out(CLK_LATCH_out));
  Clock #(.lowDuration(3)) CLK_MIR (.out(CLK_MIR_out));
  MBR_4b mbr_4b_1 (
    .Clk(CLK_MBR_REGISTERS_out), .E(mir_1_q12), .EEXIT(rxtx_transceiver_1_sext), .D(shifter_3op_4b_1_q),
    .Rd(mir_1_q11), .Wr(mir_1_q10), .S(mbr_4b_1_s), .SEXIT(mbr_4b_1_sexit));  // open: Sn
  Register_Bank_4b register_bank_4b_1 (
    .D(shifter_3op_4b_1_q), .C2(mir_1_q8), .C1(mir_1_q7), .C0(mir_1_q6), .Clk(CLK_MBR_REGISTERS_out),
    .E(mir_1_q9), .A2(mir_1_q5), .A1(mir_1_q4), .A0(mir_1_q3), .B2(mir_1_q2), .B1(mir_1_q1), .B0(mir_1_q0),
    .A(register_bank_4b_1_a), .B(register_bank_4b_1_b));
  Latch_Master_4b latch_master_4b_1 (.D(register_bank_4b_1_a), .E(CLK_LATCH_out), .Q(latch_master_4b_1_q));  // open: Qn
  A_Multiplexador_2op_4b a_multiplexador_2op_4b_1 (
    .B(mbr_4b_1_s), .op(mir_1_a19), .A(latch_master_4b_1_q), .Q(a_multiplexador_2op_4b_1_q));
  ALU_4b8op alu_4b8op_1 (.B(latch_master_4b_2_q), .op(mir_1_q16), .A(a_multiplexador_2op_4b_1_q), .Q(alu_4b8op_1_q));
  Shifter_3op_4b shifter_3op_4b_1 (.U(alu_4b8op_1_q), .op(mir_1_q14), .Q(shifter_3op_4b_1_q));
  Latch_Master_4b latch_master_4b_2 (.D(register_bank_4b_1_b), .E(CLK_LATCH_out), .Q(latch_master_4b_2_q));  // open: Qn
  MIR_Bank mir_bank_1 (
    .E1(E1), .E0(E0), .E4(E4), .E3(E3), .E2(E2), .Q1(mir_bank_1_q1), .Q2(mir_bank_1_q2), .Q3(mir_bank_1_q3),
    .Q4(mir_bank_1_q4), .Q5(mir_bank_1_q5), .Q6(mir_bank_1_q6), .Q7(mir_bank_1_q7), .Q8(mir_bank_1_q8),
    .Q9(mir_bank_1_q9), .Q10(mir_bank_1_q10), .Q11(mir_bank_1_q11), .Q12(mir_bank_1_q12),
    .Q13(mir_bank_1_q13), .Q14(mir_bank_1_q14), .Q15(mir_bank_1_q15), .Q16(mir_bank_1_q16),
    .Q17(mir_bank_1_q17), .Q18(mir_bank_1_q18), .Q19(mir_bank_1_q19), .Q20(mir_bank_1_q20),
    .Q21(mir_bank_1_q21), .Q22(mir_bank_1_q22), .Q23(mir_bank_1_q23), .Q0(mir_bank_1_q0));
  MIR mir_1 (
    .MBR(mir_bank_1_q12), .MAR(mir_bank_1_q13), .SH0(mir_bank_1_q14), .SH1(mir_bank_1_q15),
    .ALU0(mir_bank_1_q16), .ALU1(mir_bank_1_q17), .ALU2(mir_bank_1_q18), .AMUX(mir_bank_1_q19),
    .X0(mir_bank_1_q23), .DEC_B1(mir_bank_1_q1), .X1(mir_bank_1_q22), .X2(mir_bank_1_q21),
    .X3(mir_bank_1_q20), .DEC_B2(mir_bank_1_q2), .DEC_A0(mir_bank_1_q3), .DEC_A1(mir_bank_1_q4),
    .DEC_A2(mir_bank_1_q5), .DEC_C0(mir_bank_1_q6), .DEC_C1(mir_bank_1_q7), .DEC_C2(mir_bank_1_q8),
    .BR(mir_bank_1_q9), .Wr(mir_bank_1_q10), .DEC_B0(mir_bank_1_q0), .Rd(mir_bank_1_q11), .Clk(CLK_MIR_out),
    .Q12(mir_1_q12), .Q13(mir_1_q13), .Q14(mir_1_q14[0]), .Q15(mir_1_q14[1]), .Q16(mir_1_q16[0]),
    .Q17(mir_1_q16[1]), .Q18(mir_1_q16[2]), .A19(mir_1_a19), .Q1(mir_1_q1), .Q2(mir_1_q2), .Q3(mir_1_q3),
    .Q4(mir_1_q4), .Q5(mir_1_q5), .Q6(mir_1_q6), .Q7(mir_1_q7), .Q8(mir_1_q8), .Q9(mir_1_q9),
    .Q10(mir_1_q10), .Q0(mir_1_q0), .Q11(mir_1_q11));  // open: A20, A21, A22, A23
endmodule
