// Logisim project G9_Components_Basics.circ as structural Verilog: 11 circuits, main circuit Decoder_4op_1b_2x4
module A_Decoder_2op_1b_1x2 (
  input  op,
  output m0,
  output m1
);

  buf buffer_1 (m1, op);
  not not_1 (m0, op);
endmodule

module A_Multiplexador_2op_1b (
  input  i0,
  input  i1,
  input  op,
  output Q
);

  wire a_decoder_2op_1b_1x2_1_m0, a_decoder_2op_1b_1x2_1_m1, and_1_out, and_2_out;

  A_Decoder_2op_1b_1x2 a_decoder_2op_1b_1x2_1 (.op(op), .m0(a_decoder_2op_1b_1x2_1_m0), .m1(a_decoder_2op_1b_1x2_1_m1));
  and and_1 (and_1_out, a_decoder_2op_1b_1x2_1_m0, i0);
  or or_1 (Q, and_1_out, and_2_out);
  and and_2 (and_2_out, a_decoder_2op_1b_1x2_1_m1, i1);
endmodule

module A_Multiplexador_2op_4b (
  input  [3:0] A,
  input  [3:0] B,
  input  op,
  output [3:0] Q
);

  A_Multiplexador_2op_1b a_multiplexador_2op_1b_1 (.op(op), .i0(A[0]), .i1(B[0]), .Q(Q[0]));
  A_Multiplexador_2op_1b a_multiplexador_2op_1b_2 (.op(op), .i0(A[1]), .i1(B[1]), .Q(Q[1]));
  A_Multiplexador_2op_1b a_multiplexador_2op_1b_3 (.op(op), .i0(A[2]), .i1(B[2]), .Q(Q[2]));
  A_Multiplexador_2op_1b a_multiplexador_2op_1b_4 (.op(op), .i0(A[3]), .i1(B[3]), .Q(Q[3]));
endmodule

module Decoder_4op_1b_2x4 (
  input  [1:0] op,
  output m0,
  output m1,
  output m2,
  output m3
);

  wire buffer_1_out, buffer_2_out, not_1_out, not_2_out;

  buf buffer_1 (buffer_1_out, op[0]);
  buf buffer_2 (buffer_2_out, op[1]);
  not not_1 (not_1_out, op[0]);
  not not_2 (not_2_out, op[1]);
  and and_1 (m0, not_1_out, not_2_out);
  and and_2 (m1, buffer_1_out, not_2_out);
  and and_3 (m2, not_1_out, buffer_2_out);
  and and_4 (m3, buffer_1_out, buffer_2_out);
endmodule

module Multiplexador_4op_1b (
  input  i0,
  input  i1,
  input  i2,
  input  i3,
  input  [1:0] op,
  output Q
);

  wire and_1_out, and_2_out, and_3_out, and_4_out, decoder_4op_1b_2x4_1_m0, decoder_4op_1b_2x4_1_m1,
       decoder_4op_1b_2x4_1_m2, decoder_4op_1b_2x4_1_m3;

  Decoder_4op_1b_2x4 decoder_4op_1b_2x4_1 (
    .op(op), .m0(decoder_4op_1b_2x4_1_m0), .m1(decoder_4op_1b_2x4_1_m1), .m2(decoder_4op_1b_2x4_1_m2),
    .m3(decoder_4op_1b_2x4_1_m3));
  and and_1 (and_1_out, decoder_4op_1b_2x4_1_m0, i0);
  and and_2 (and_2_out, decoder_4op_1b_2x4_1_m1, i1);
  and and_3 (and_3_out, decoder_4op_1b_2x4_1_m2, i2);
  or or_1 (Q, and_1_out, and_2_out, and_3_out, and_4_out);
  and and_4 (and_4_out, decoder_4op_1b_2x4_1_m3, i3);
endmodule

module Multiplexador_4op_4b (
  input  [3:0] A,
  input  [3:0] B,
  input  [3:0] C,
  input  [3:0] D,
  input  [1:0] op,
  output [3:0] Q
);

  Multiplexador_4op_1b multiplexador_4op_1b_1 (.op(op), .i3(D[0]), .i0(A[0]), .i1(B[0]), .i2(C[0]), .Q(Q[0]));
  Multiplexador_4op_1b multiplexador_4op_1b_2 (.op(op), .i3(D[1]), .i0(A[1]), .i1(B[1]), .i2(C[1]), .Q(Q[1]));
  Multiplexador_4op_1b multiplexador_4op_1b_3 (.op(op), .i3(D[2]), .i0(A[2]), .i1(B[2]), .i2(C[2]), .Q(Q[2]));
  Multiplexador_4op_1b multiplexador_4op_1b_4 (.op(op), .i3(D[3]), .i0(A[3]), .i1(B[3]), .i2(C[3]), .Q(Q[3]));
endmodule

module Decoder_8op_3x8 (
  input  [2:0] op,
  output m0,
  output m1,
  output m2,
  output m3,
  output m4,
  output m5,
  output m6,
  output m7
);

  wire buffer_1_out, buffer_2_out, buffer_3_out, not_1_out, not_2_out, not_3_out;

  buf buffer_1 (buffer_1_out, op[1]);
  buf buffer_2 (buffer_2_out, op[2]);
  buf buffer_3 (buffer_3_out, op[0]);
  not not_1 (not_1_out, op[1]);
  not not_2 (not_2_out, op[2]);
  not not_3 (not_3_out, op[0]);
  and and_1 (m0, not_3_out, not_1_out, not_2_out);
  and and_2 (m1, buffer_3_out, not_2_out, not_1_out);
  and and_3 (m2, not_2_out, buffer_1_out, not_3_out);
  and and_4 (m3, buffer_3_out, buffer_1_out, not_2_out);
  and and_5 (m4, not_3_out, not_1_out, buffer_2_out);
  and and_6 (m5, buffer_3_out, not_1_out, buffer_2_out);
  and and_7 (m6, not_3_out, buffer_1_out, buffer_2_out);
  and and_8 (m7, buffer_3_out, buffer_1_out, buffer_2_out);
endmodule

module Multiplexador_8op_1b (
  input  i0,
  input  i1,
  input  i2,
  input  i3,
  input  i4,
  input  i5,
  input  i6,
  input  i7,
  input  [2:0] op,
  output Q
);

  wire and_1_out, and_2_out, and_3_out, and_4_out, and_5_out, and_6_out, and_7_out, and_8_out,
       decoder_8op_3x8_1_m0, decoder_8op_3x8_1_m1, decoder_8op_3x8_1_m2, decoder_8op_3x8_1_m3,
       decoder_8op_3x8_1_m4, decoder_8op_3x8_1_m5, decoder_8op_3x8_1_m6, decoder_8op_3x8_1_m7, or_1_out,
       or_3_out;

  Decoder_8op_3x8 decoder_8op_3x8_1 (
    .op(op), .m0(decoder_8op_3x8_1_m0), .m1(decoder_8op_3x8_1_m1), .m2(decoder_8op_3x8_1_m2),
    .m3(decoder_8op_3x8_1_m3), .m4(decoder_8op_3x8_1_m4), .m5(decoder_8op_3x8_1_m5),
    .m6(decoder_8op_3x8_1_m6), .m7(decoder_8op_3x8_1_m7));
  and and_1 (and_1_out, decoder_8op_3x8_1_m0, i0);
  and and_2 (and_2_out, decoder_8op_3x8_1_m1, i1);
  and and_3 (and_3_out, decoder_8op_3x8_1_m2, i2);
  or or_1 (or_1_out, and_1_out, and_2_out, and_3_out, and_4_out);
  and and_4 (and_4_out, decoder_8op_3x8_1_m3, i3);
  and and_5 (and_5_out, decoder_8op_3x8_1_m4, i4);
  or or_2 (Q, or_1_out, or_3_out);
  and and_6 (and_6_out, decoder_8op_3x8_1_m5, i5);
  and and_7 (and_7_out, decoder_8op_3x8_1_m6, i6);
  or or_3 (or_3_out, and_5_out, and_6_out, and_7_out, and_8_out);
  and and_8 (and_8_out, decoder_8op_3x8_1_m7, i7);
endmodule

module Multiplexador_8op_4b (
  input  [3:0] A,
  input  [3:0] B,
  input  [3:0] C,
  input  [3:0] D,
  input  [2:0] op,
  input  [3:0] E,
  input  [3:0] F,
  input  [3:0] G,
  input  [3:0] H,
  output [3:0] Q
);

  Multiplexador_8op_1b multiplexador_8op_1b_1 (
    .op(op), .i3(D[0]), .i4(E[0]), .i5(F[0]), .i6(G[0]), .i7(H[0]), .i0(A[0]), .i1(B[0]), .i2(C[0]), .Q(Q[0]));
  Multiplexador_8op_1b multiplexador_8op_1b_2 (
    .op(op), .i3(D[1]), .i4(E[1]), .i5(F[1]), .i6(G[1]), .i7(H[1]), .i0(A[1]), .i1(B[1]), .i2(C[1]), .Q(Q[1]));
  Multiplexador_8op_1b multiplexador_8op_1b_3 (
    .op(op), .i3(D[2]), .i4(E[2]), .i5(F[2]), .i6(G[2]), .i7(H[2]), .i0(A[2]), .i1(B[2]), .i2(C[2]), .Q(Q[2]));
  Multiplexador_8op_1b multiplexador_8op_1b_4 (
    .op(op), .i3(D[3]), .i4(E[3]), .i5(F[3]), .i6(G[3]), .i7(H[3]), .i0(A[3]), .i1(B[3]), .i2(C[3]), .Q(Q[3]));
endmodule

module Shifter_3op_4b (
  input  [3:0] U,
  input  [1:0] op,
  output [3:0] Q
);

  wire [1:0] handler_4op_to_3op_1_tr;

  Handler_4op_to_3op handler_4op_to_3op_1 (.op(op), .tr(handler_4op_to_3op_1_tr));
  Multiplexador_4op_1b multiplexador_4op_1b_1 (
    .op(handler_4op_to_3op_1_tr), .i3(1'b0), .i0(U[3]), .i1(1'b0), .i2(U[2]), .Q(Q[3]));
  Multiplexador_4op_1b multiplexador_4op_1b_2 (
    .op(handler_4op_to_3op_1_tr), .i3(1'b0), .i0(U[2]), .i1(U[3]), .i2(U[1]), .Q(Q[2]));
  Multiplexador_4op_1b multiplexador_4op_1b_3 (
    .op(handler_4op_to_3op_1_tr), .i3(1'b0), .i0(U[1]), .i1(U[2]), .i2(U[0]), .Q(Q[1]));
  Multiplexador_4op_1b multiplexador_4op_1b_4 (
    .op(handler_4op_to_3op_1_tr), .i3(1'b0), .i0(U[0]), .i1(U[1]), .i2(1'b0), .Q(Q[0]));
endmodule

module Handler_4op_to_3op (
  input  [1:0] op,
  output [1:0] tr
);

  wire buffer_1_out, buffer_2_out, not_1_out, not_2_out;

  buf buffer_1 (buffer_1_out, op[0]);
  not not_1 (not_1_out, op[0]);
  buf buffer_2 (buffer_2_out, op[1]);
  not not_2 (not_2_out, op[1]);
  and and_1 (tr[0], buffer_1_out, not_2_out);
  and and_2 (tr[1], buffer_2_out, not_1_out);
endmodule
