// Logisim project G9_Registers_Memorys.circ as structural Verilog: 19 circuits, main circuit Latch_Master_1b
module Latch_Master_1b (
  input  D,
  input  E,
  output Q,
  output Qn
);

  wire nand_1_out, nand_2_out, nand_3_out;

  nand nand_1 (nand_1_out, D, D);
  nand nand_2 (nand_2_out, D, E);
  nand nand_3 (nand_3_out, E, nand_1_out);
  nand nand_4 (Q, nand_2_out, Qn);
  nand nand_5 (Qn, Q, nand_3_out);

  // Notes on the sheet:
  //   E D Q Q'
  //   0 0 Hold Hold'
  //   0 1 Hold Hold'
  //   1 0 Reset Set
  //   1 1 Set Reset
  //   Tipo D
  //   D = Data
  //   E = Enable (clock)
  //   Ctrl
  //   Q' = Qn ( !Q )
  //   Memoria
endmodule

module Latch_Slave_1b (
  input  D,
  input  E,
  input  R,
  output Q,
  output Qn
);

  wire nand_1_out, nand_2_out;

  nand nand_1 (nand_1_out, D, E);
  nand nand_2 (nand_2_out, E, R);
  nand nand_3 (Q, nand_1_out, Qn);
  nand nand_4 (Qn, Q, nand_2_out);

  // Notes on the sheet:
  //   Ctrl
  //   Memoria
endmodule

module Latch_Master_4b (
  input  [3:0] D,
  input  E,
  output [3:0] Q,
  output [3:0] Qn
);

  Latch_Master_1b latch_master_1b_1 (.D(D[3]), .E(E), .Qn(Qn[3]), .Q(Q[3]));
  Latch_Master_1b latch_master_1b_2 (.D(D[2]), .E(E), .Qn(Qn[2]), .Q(Q[2]));
  Latch_Master_1b latch_master_1b_3 (.D(D[1]), .E(E), .Qn(Qn[1]), .Q(Q[1]));
  Latch_Master_1b latch_master_1b_4 (.D(D[0]), .E(E), .Qn(Qn[0]), .Q(Q[0]));
endmodule

module Latch_Slave_4b (
  input  [3:0] D,
  input  E,
  input  R,
  output [3:0] Q,
  output [3:0] Qn
);

  Latch_Slave_1b latch_slave_1b_1 (.R(R), .D(D[3]), .E(E), .Qn(Qn[3]), .Q(Q[3]));
  Latch_Slave_1b latch_slave_1b_2 (.R(R), .D(D[2]), .E(E), .Qn(Qn[2]), .Q(Q[2]));
  Latch_Slave_1b latch_slave_1b_3 (.R(R), .D(D[1]), .E(E), .Qn(Qn[1]), .Q(Q[1]));
  Latch_Slave_1b latch_slave_1b_4 (.R(R), .D(D[0]), .E(E), .Qn(Qn[0]), .Q(Q[0]));
endmodule

module FlipFlopD_1b (
  input  D,
  input  E,
  input  R,
  output Q,
  output Qn
);

  wire Master_Latcher_q, not_1_out;

  not not_1 (not_1_out, E);
  Latch_Master_1b Master_Latcher (.D(D), .E(E), .Q(Master_Latcher_q));  // open: Qn
  Latch_Slave_1b Slave_Latcher (.R(not_1_out), .D(Master_Latcher_q), .E(R), .Qn(Qn), .Q(Q));
endmodule

module FlipFlopD_4b (
  input  [3:0] D,
  input  E,
  input  R,
  output [3:0] Q,
  output [3:0] Qn
);

  FlipFlopD_1b flipflopd_1b_1 (.E(E), .R(R), .D(D[3]), .Qn(Qn[3]), .Q(Q[3]));
  FlipFlopD_1b flipflopd_1b_2 (.E(E), .R(R), .D(D[2]), .Qn(Qn[2]), .Q(Q[2]));
  FlipFlopD_1b flipflopd_1b_3 (.E(E), .R(R), .D(D[1]), .Qn(Qn[1]), .Q(Q[1]));
  FlipFlopD_1b flipflopd_1b_4 (.E(E), .R(R), .D(D[0]), .Qn(Qn[0]), .Q(Q[0]));
endmodule

module MAR_HomeMade (
  input  [3:0] D,
  input  Clock,
  input  E,
  input  R,
  output [3:0] A,
  output [3:0] An
);

  wire and_1_out, and_2_out, and_3_out, and_4_out;

  and and_1 (and_1_out, Clock, E);
  and and_2 (and_2_out, Clock, E);
  and and_3 (and_3_out, Clock, E);
  and and_4 (and_4_out, Clock, E);
  FlipFlopD_1b flipflopd_1b_1 (.E(and_1_out), .R(R), .D(D[3]), .Qn(An[3]), .Q(A[3]));
  FlipFlopD_1b flipflopd_1b_2 (.E(and_2_out), .R(R), .D(D[2]), .Qn(An[2]), .Q(A[2]));
  FlipFlopD_1b flipflopd_1b_3 (.E(and_3_out), .R(R), .D(D[1]), .Qn(An[1]), .Q(A[1]));
  FlipFlopD_1b flipflopd_1b_4 (.E(and_4_out), .R(R), .D(D[0]), .Qn(An[0]), .Q(A[0]));
endmodule

module MAR_4b (
  input  [3:0] D,
  input  Clock,
  input  E,
  input  R,
  output [3:0] A,
  output [3:0] An
);

  wire and_1_out, and_2_out, and_3_out, and_4_out;

  and and_1 (and_1_out, Clock, E);
  and and_2 (and_2_out, Clock, E);
  and and_3 (and_3_out, Clock, E);
  and and_4 (and_4_out, Clock, E);
  D_Flip_Flop d_ff_1 (.D(D[3]), .clk(and_1_out), .Q(A[3]), .Qn(An[3]), .reset(R));  // open: preset
  D_Flip_Flop d_ff_2 (.D(D[3]), .clk(and_2_out), .Q(A[2]), .Qn(An[2]), .reset(R));  // open: preset
  D_Flip_Flop d_ff_3 (.D(D[3]), .clk(and_3_out), .Q(A[1]), .Qn(An[1]), .reset(R));  // open: preset
  D_Flip_Flop d_ff_4 (.D(D[3]), .clk(and_4_out), .Q(A[0]), .Qn(An[0]), .reset(R));  // open: preset
endmodule

module MBR_4b_Pure (
  input  [3:0] D,
  input  [3:0] EEXIT,
  input  Clk,
  input  E,
  input  Rd,
  input  Wr,
  output [3:0] S,
  output [3:0] SEXIT
);

  wire and_1_out, buffer_tristate_ah_1b_1_q, buffer_tristate_ah_1b_5_q, buffer_tristate_ah_1b_8_q,
       buffer_tristate_ah_1b_13_q, d_ff_1_q, d_ff_2_q, d_ff_3_q, d_ff_4_q, decoder_4op_1b_2x4_1_m0,
       decoder_4op_1b_2x4_1_m1, decoder_4op_1b_2x4_1_m2, or_1_out, or_2_out, or_3_out, or_4_out, or_5_out,
       or_6_out, or_7_out, or_8_out;
  wire [1:0] handler_4op_to_3op_1_tr;

  and and_1 (and_1_out, Clk, E);
  Decoder_4op_1b_2x4 decoder_4op_1b_2x4_1 (
    .op(handler_4op_to_3op_1_tr), .m0(decoder_4op_1b_2x4_1_m0), .m1(decoder_4op_1b_2x4_1_m1),
    .m2(decoder_4op_1b_2x4_1_m2));  // open: m3
  Handler_4op_to_3op handler_4op_to_3op_1 (.op({Wr, Rd}), .tr(handler_4op_to_3op_1_tr));
  Buffer_TriState_AH_1b buffer_tristate_ah_1b_1 (.A(D[3]), .Ctrl(or_1_out), .Q(buffer_tristate_ah_1b_1_q));
  or or_1 (or_1_out, decoder_4op_1b_2x4_1_m0, decoder_4op_1b_2x4_1_m1);
  Buffer_TriState_AH_1b buffer_tristate_ah_1b_2 (
    .A(EEXIT[3]), .Ctrl(decoder_4op_1b_2x4_1_m2), .Q(buffer_tristate_ah_1b_1_q));
  D_Flip_Flop d_ff_1 (.D(buffer_tristate_ah_1b_1_q), .clk(and_1_out), .Q(d_ff_1_q));  // open: Qn, preset, reset
  Buffer_TriState_AH_1b buffer_tristate_ah_1b_3 (.A(d_ff_1_q), .Ctrl(or_2_out), .Q(S[3]));
  or or_2 (or_2_out, decoder_4op_1b_2x4_1_m0, decoder_4op_1b_2x4_1_m2);
  Buffer_TriState_AH_1b buffer_tristate_ah_1b_4 (.A(d_ff_1_q), .Ctrl(decoder_4op_1b_2x4_1_m2), .Q(SEXIT[3]));
  Buffer_TriState_AH_1b buffer_tristate_ah_1b_5 (.A(D[2]), .Ctrl(or_3_out), .Q(buffer_tristate_ah_1b_5_q));
  Buffer_TriState_AH_1b buffer_tristate_ah_1b_6 (
    .A(EEXIT[2]), .Ctrl(decoder_4op_1b_2x4_1_m2), .Q(buffer_tristate_ah_1b_5_q));
  or or_3 (or_3_out, decoder_4op_1b_2x4_1_m0, decoder_4op_1b_2x4_1_m1);
  D_Flip_Flop d_ff_2 (.D(buffer_tristate_ah_1b_5_q), .clk(and_1_out), .Q(d_ff_2_q));  // open: Qn, preset, reset
  Buffer_TriState_AH_1b buffer_tristate_ah_1b_7 (.A(d_ff_2_q), .Ctrl(or_4_out), .Q(S[2]));
  or or_4 (or_4_out, decoder_4op_1b_2x4_1_m0, decoder_4op_1b_2x4_1_m2);
  Buffer_TriState_AH_1b buffer_tristate_ah_1b_8 (.A(D[1]), .Ctrl(or_5_out), .Q(buffer_tristate_ah_1b_8_q));
  Buffer_TriState_AH_1b buffer_tristate_ah_1b_9 (.A(d_ff_2_q), .Ctrl(decoder_4op_1b_2x4_1_m2), .Q(SEXIT[2]));
  Buffer_TriState_AH_1b buffer_tristate_ah_1b_10 (
    .A(EEXIT[1]), .Ctrl(decoder_4op_1b_2x4_1_m2), .Q(buffer_tristate_ah_1b_8_q));
  or or_5 (or_5_out, decoder_4op_1b_2x4_1_m0, decoder_4op_1b_2x4_1_m1);
  D_Flip_Flop d_ff_3 (.D(buffer_tristate_ah_1b_8_q), .clk(and_1_out), .Q(d_ff_3_q));  // open: Qn, preset, reset
  Buffer_TriState_AH_1b buffer_tristate_ah_1b_11 (.A(d_ff_3_q), .Ctrl(decoder_4op_1b_2x4_1_m2), .Q(SEXIT[1]));
  Buffer_TriState_AH_1b buffer_tristate_ah_1b_12 (.A(d_ff_3_q), .Ctrl(or_6_out), .Q(S[1]));
  or or_6 (or_6_out, decoder_4op_1b_2x4_1_m0, decoder_4op_1b_2x4_1_m2);
  Buffer_TriState_AH_1b buffer_tristate_ah_1b_13 (.A(D[0]), .Ctrl(or_7_out), .Q(buffer_tristate_ah_1b_13_q));
  or or_7 (or_7_out, decoder_4op_1b_2x4_1_m0, decoder_4op_1b_2x4_1_m1);
  Buffer_TriState_AH_1b buffer_tristate_ah_1b_14 (
    .A(EEXIT[0]), .Ctrl(decoder_4op_1b_2x4_1_m2), .Q(buffer_tristate_ah_1b_13_q));
  D_Flip_Flop d_ff_4 (.D(buffer_tristate_ah_1b_13_q), .clk(and_1_out), .Q(d_ff_4_q));  // open: Qn, preset, reset
  Buffer_TriState_AH_1b buffer_tristate_ah_1b_15 (.A(d_ff_4_q), .Ctrl(or_8_out), .Q(S[0]));
  Buffer_TriState_AH_1b buffer_tristate_ah_1b_16 (.A(d_ff_4_q), .Ctrl(decoder_4op_1b_2x4_1_m2), .Q(SEXIT[0]));
  or or_8 (or_8_out, decoder_4op_1b_2x4_1_m0, decoder_4op_1b_2x4_1_m2);
endmodule

module MBR_4b (
  input  [3:0] D,
  input  [3:0] EEXIT,
  input  Clk,
  input  E,
  input  Rd,
  input  Wr,
  output [3:0] S,
  output [3:0] Sn,
  output [3:0] SEXIT
);

  wire and_1_out, decoder_4op_1b_2x4_1_m0, decoder_4op_1b_2x4_1_m1, decoder_4op_1b_2x4_1_m2,
       handler_mbr_1_sm0, handler_mbr_1_sm1, handler_mbr_1_sm2, handler_mbr_2_sm0, handler_mbr_2_sm1,
       handler_mbr_2_sm2, handler_mbr_3_sm0, handler_mbr_3_sm1, handler_mbr_3_sm2, handler_mbr_4_sm0,
       handler_mbr_4_sm1, handler_mbr_4_sm2;
  wire [1:0] handler_4op_to_3op_1_tr;

  and and_1 (and_1_out, Clk, E);
  Decoder_4op_1b_2x4 decoder_4op_1b_2x4_1 (
    .op(handler_4op_to_3op_1_tr), .m0(decoder_4op_1b_2x4_1_m0), .m1(decoder_4op_1b_2x4_1_m1),
    .m2(decoder_4op_1b_2x4_1_m2));  // open: m3
  Handler_4op_to_3op handler_4op_to_3op_1 (.op({Wr, Rd}), .tr(handler_4op_to_3op_1_tr));
  Handler_MBR handler_mbr_1 (
    .D(D[3]), .EE(EEXIT[3]), .ClkE(and_1_out), .m1(decoder_4op_1b_2x4_1_m1), .m2(decoder_4op_1b_2x4_1_m2),
    .m0(decoder_4op_1b_2x4_1_m0), .S(S[3]), .Sn(Sn[3]), .SE(SEXIT[3]), .sm1(handler_mbr_1_sm1),
    .sm2(handler_mbr_1_sm2), .sm0(handler_mbr_1_sm0));
  Handler_MBR handler_mbr_2 (
    .D(D[2]), .EE(EEXIT[2]), .ClkE(and_1_out), .m1(handler_mbr_1_sm1), .m2(handler_mbr_1_sm2),
    .m0(handler_mbr_1_sm0), .S(S[2]), .Sn(Sn[2]), .SE(SEXIT[2]), .sm1(handler_mbr_2_sm1),
    .sm2(handler_mbr_2_sm2), .sm0(handler_mbr_2_sm0));
  Handler_MBR handler_mbr_3 (
    .D(D[1]), .EE(EEXIT[1]), .ClkE(and_1_out), .m1(handler_mbr_2_sm1), .m2(handler_mbr_2_sm2),
    .m0(handler_mbr_2_sm0), .S(S[1]), .Sn(Sn[1]), .SE(SEXIT[1]), .sm1(handler_mbr_3_sm1),
    .sm2(handler_mbr_3_sm2), .sm0(handler_mbr_3_sm0));
  Handler_MBR handler_mbr_4 (
    .D(D[0]), .EE(EEXIT[0]), .ClkE(and_1_out), .m1(handler_mbr_3_sm1), .m2(handler_mbr_3_sm2),
    .m0(handler_mbr_3_sm0), .S(S[0]), .Sn(Sn[0]), .SE(SEXIT[0]), .sm1(handler_mbr_4_sm1),
    .sm2(handler_mbr_4_sm2), .sm0(handler_mbr_4_sm0));
endmodule

module Handler_MBR (
  input  m0,
  input  m1,
  input  m2,
  input  D,
  input  EE,
  input  ClkE,
  output S,
  output Sn,
  output SE,
  output sm0,
  output sm1,
  output sm2
);

  wire buffer_tristate_ah_1b_1_q, d_ff_1_q, d_ff_1_qn, or_1_out, or_2_out;

  or or_1 (or_1_out, m0, m1);
  Buffer_TriState_AH_1b buffer_tristate_ah_1b_1 (.A(D), .Ctrl(or_1_out), .Q(buffer_tristate_ah_1b_1_q));
  Buffer_TriState_AH_1b buffer_tristate_ah_1b_2 (.A(EE), .Ctrl(m2), .Q(buffer_tristate_ah_1b_1_q));
  D_Flip_Flop d_ff_1 (.D(buffer_tristate_ah_1b_1_q), .clk(ClkE), .Q(d_ff_1_q), .Qn(d_ff_1_qn));  // open: preset, reset
  or or_2 (or_2_out, m0, m2);
  Buffer_TriState_AH_1b buffer_tristate_ah_1b_3 (.A(d_ff_1_q), .Ctrl(or_2_out), .Q(S));
  Buffer_TriState_AH_1b buffer_tristate_ah_1b_4 (.A(d_ff_1_q), .Ctrl(m1), .Q(SE));
  Buffer_TriState_AH_1b buffer_tristate_ah_1b_5 (.A(d_ff_1_qn), .Ctrl(or_2_out), .Q(Sn));

  assign sm0 = m0;
  assign sm1 = m1;
  assign sm2 = m2;
endmodule

module Register_4b (
  input  [3:0] C,
  input  ClkE,
  input  E1,
  input  E0,
  output [3:0] A,
  output [3:0] B
);

  wire d_ff_1_q, d_ff_2_q, d_ff_3_q, d_ff_4_q, handler_register_1_e0s, handler_register_1_e1s,
       handler_register_2_e0s, handler_register_2_e1s, handler_register_3_e0s, handler_register_3_e1s,
       handler_register_4_e0s, handler_register_4_e1s;

  D_Flip_Flop d_ff_1 (.D(C[0]), .clk(ClkE), .Q(d_ff_1_q));  // open: Qn, preset, reset
  D_Flip_Flop d_ff_2 (.D(C[1]), .clk(ClkE), .Q(d_ff_2_q));  // open: Qn, preset, reset
  D_Flip_Flop d_ff_3 (.D(C[2]), .clk(ClkE), .Q(d_ff_3_q));  // open: Qn, preset, reset
  D_Flip_Flop d_ff_4 (.D(C[3]), .clk(ClkE), .Q(d_ff_4_q));  // open: Qn, preset, reset
  Handler_Register handler_register_1 (
    .E0(E0), .c(d_ff_1_q), .E1(E1), .e0s(handler_register_1_e0s), .b(B[0]), .a(A[0]),
    .e1s(handler_register_1_e1s));
  Handler_Register handler_register_2 (
    .E0(handler_register_1_e0s), .c(d_ff_2_q), .E1(handler_register_1_e1s), .e0s(handler_register_2_e0s),
    .b(B[1]), .a(A[1]), .e1s(handler_register_2_e1s));
  Handler_Register handler_register_3 (
    .E0(handler_register_2_e0s), .c(d_ff_3_q), .E1(handler_register_2_e1s), .e0s(handler_register_3_e0s),
    .b(B[2]), .a(A[2]), .e1s(handler_register_3_e1s));
  Handler_Register handler_register_4 (
    .E0(handler_register_3_e0s), .c(d_ff_4_q), .E1(handler_register_3_e1s), .e0s(handler_register_4_e0s),
    .b(B[3]), .a(A[3]), .e1s(handler_register_4_e1s));
endmodule

module Handler_Register (
  input  E1,
  input  E0,
  input  c,
  output a,
  output b,
  output e1s,
  output e0s
);

  Buffer_TriState_AH_1b buffer_tristate_ah_1b_1 (.A(c), .Ctrl(E1), .Q(a));
  Buffer_TriState_AH_1b buffer_tristate_ah_1b_2 (.A(c), .Ctrl(E0), .Q(b));

  assign e0s = E0;
  assign e1s = E1;
endmodule

module Register_Bank_4b (
  input  C2,
  input  C1,
  input  C0,
  input  A2,
  input  A1,
  input  A0,
  input  B2,
  input  B1,
  input  B0,
  input  Clk,
  input  E,
  input  [3:0] D,
  output [3:0] A,
  output [3:0] B
);

  wire and_1_out, and_2_out, and_3_out, and_4_out, and_5_out, and_6_out, and_7_out, and_8_out, and_9_out,
       decoder_8op_3x8_1_m0, decoder_8op_3x8_1_m1, decoder_8op_3x8_1_m2, decoder_8op_3x8_1_m3,
       decoder_8op_3x8_1_m4, decoder_8op_3x8_1_m5, decoder_8op_3x8_1_m6, decoder_8op_3x8_1_m7,
       decoder_8op_3x8_2_m0, decoder_8op_3x8_2_m1, decoder_8op_3x8_2_m2, decoder_8op_3x8_2_m3,
       decoder_8op_3x8_2_m4, decoder_8op_3x8_2_m5, decoder_8op_3x8_2_m6, decoder_8op_3x8_2_m7,
       decoder_8op_3x8_3_m0, decoder_8op_3x8_3_m1, decoder_8op_3x8_3_m2, decoder_8op_3x8_3_m3,
       decoder_8op_3x8_3_m4, decoder_8op_3x8_3_m5, decoder_8op_3x8_3_m6, decoder_8op_3x8_3_m7;

  Decoder_8op_3x8 decoder_8op_3x8_1 (
    .op({C2, C1, C0}), .m0(decoder_8op_3x8_1_m0), .m1(decoder_8op_3x8_1_m1), .m2(decoder_8op_3x8_1_m2),
    .m3(decoder_8op_3x8_1_m3), .m4(decoder_8op_3x8_1_m4), .m5(decoder_8op_3x8_1_m5),
    .m6(decoder_8op_3x8_1_m6), .m7(decoder_8op_3x8_1_m7));
  and and_1 (and_1_out, Clk, E);
  and and_2 (and_2_out, decoder_8op_3x8_1_m0, and_1_out);
  and and_3 (and_3_out, decoder_8op_3x8_1_m1, and_1_out);
  and and_4 (and_4_out, decoder_8op_3x8_1_m2, and_1_out);
  and and_5 (and_5_out, decoder_8op_3x8_1_m3, and_1_out);
  and and_6 (and_6_out, decoder_8op_3x8_1_m4, and_1_out);
  and and_7 (and_7_out, decoder_8op_3x8_1_m5, and_1_out);
  and and_8 (and_8_out, decoder_8op_3x8_1_m6, and_1_out);
  and and_9 (and_9_out, decoder_8op_3x8_1_m7, and_1_out);
  Register_4b R0 (.C(D), .ClkE(and_2_out), .E1(decoder_8op_3x8_2_m0), .E0(decoder_8op_3x8_3_m0), .A(A), .B(B));
  Register_4b R1 (.C(D), .ClkE(and_3_out), .E1(decoder_8op_3x8_2_m1), .E0(decoder_8op_3x8_3_m1), .A(A), .B(B));
  Register_4b R2 (.C(D), .ClkE(and_4_out), .E1(decoder_8op_3x8_2_m2), .E0(decoder_8op_3x8_3_m2), .A(A), .B(B));
  Register_4b R3 (.C(D), .ClkE(and_5_out), .E1(decoder_8op_3x8_2_m3), .E0(decoder_8op_3x8_3_m3), .A(A), .B(B));
  Register_4b R4 (.C(D), .ClkE(and_6_out), .E1(decoder_8op_3x8_2_m4), .E0(decoder_8op_3x8_3_m4), .A(A), .B(B));
  Register_4b R5 (.C(D), .ClkE(and_7_out), .E1(decoder_8op_3x8_2_m5), .E0(decoder_8op_3x8_3_m5), .A(A), .B(B));
  Register_4b R6 (.C(D), .ClkE(and_8_out), .E1(decoder_8op_3x8_2_m6), .E0(decoder_8op_3x8_3_m6), .A(A), .B(B));
  Register_4b R7 (.C(D), .ClkE(and_9_out), .E1(decoder_8op_3x8_2_m7), .E0(decoder_8op_3x8_3_m7), .A(A), .B(B));
  Decoder_8op_3x8 decoder_8op_3x8_2 (
    .op({A2, A1, A0}), .m0(decoder_8op_3x8_2_m0), .m1(decoder_8op_3x8_2_m1), .m2(decoder_8op_3x8_2_m2),
    .m3(decoder_8op_3x8_2_m3), .m4(decoder_8op_3x8_2_m4), .m5(decoder_8op_3x8_2_m5),
    .m6(decoder_8op_3x8_2_m6), .m7(decoder_8op_3x8_2_m7));
  Decoder_8op_3x8 decoder_8op_3x8_3 (
    .op({B2, B1, B0}), .m0(decoder_8op_3x8_3_m0), .m1(decoder_8op_3x8_3_m1), .m2(decoder_8op_3x8_3_m2),
    .m3(decoder_8op_3x8_3_m3), .m4(decoder_8op_3x8_3_m4), .m5(decoder_8op_3x8_3_m5),
    .m6(decoder_8op_3x8_3_m6), .m7(decoder_8op_3x8_3_m7));
endmodule

module RxTx_Transceiver (
  input  [3:0] TEC,
  input  [3:0] BusExt,
  input  T_R,
  output [3:0] DIS,
  output [3:0] SExt
);

  wire a_decoder_2op_1b_1x2_1_m0, a_decoder_2op_1b_1x2_1_m1;
  wire [3:0] buffer_tristate_ah_4b_1_q, buffer_tristate_ah_4b_2_q;

  A_Decoder_2op_1b_1x2 a_decoder_2op_1b_1x2_1 (
    .op(T_R), .m0(a_decoder_2op_1b_1x2_1_m0), .m1(a_decoder_2op_1b_1x2_1_m1));
  Buffer_TriState_AH_1b buffer_tristate_ah_1b_1 (.A(TEC[3]), .Ctrl(a_decoder_2op_1b_1x2_1_m0), .Q(SExt[3]));
  Buffer_TriState_AH_1b buffer_tristate_ah_1b_2 (.A(TEC[2]), .Ctrl(a_decoder_2op_1b_1x2_1_m0), .Q(SExt[2]));
  Buffer_TriState_AH_1b buffer_tristate_ah_1b_3 (.A(TEC[1]), .Ctrl(a_decoder_2op_1b_1x2_1_m0), .Q(SExt[1]));
  Buffer_TriState_AH_1b buffer_tristate_ah_1b_4 (.A(TEC[0]), .Ctrl(a_decoder_2op_1b_1x2_1_m0), .Q(SExt[0]));
  Buffer_TriState_AH_1b buffer_tristate_ah_1b_5 (.A(BusExt[3]), .Ctrl(a_decoder_2op_1b_1x2_1_m1), .Q(DIS[3]));
  Buffer_TriState_AH_1b buffer_tristate_ah_1b_6 (.A(BusExt[2]), .Ctrl(a_decoder_2op_1b_1x2_1_m1), .Q(DIS[2]));
  Buffer_TriState_AH_1b buffer_tristate_ah_1b_7 (.A(BusExt[1]), .Ctrl(a_decoder_2op_1b_1x2_1_m1), .Q(DIS[1]));
  Buffer_TriState_AH_1b buffer_tristate_ah_1b_8 (.A(BusExt[0]), .Ctrl(a_decoder_2op_1b_1x2_1_m1), .Q(DIS[0]));
  Buffer_TriState_AH_4b buffer_tristate_ah_4b_1 (
    .Ctrl(a_decoder_2op_1b_1x2_1_m0), .A(TEC), .Q(buffer_tristate_ah_4b_1_q));
  Buffer_TriState_AH_4b buffer_tristate_ah_4b_2 (
    .Ctrl(a_decoder_2op_1b_1x2_1_m1), .A(BusExt), .Q(buffer_tristate_ah_4b_2_q));
  Hex_Digit_Display hex_digit_display_1 (.value(buffer_tristate_ah_4b_1_q));  // open: dp
  Hex_Digit_Display hex_digit_display_2 (.value(buffer_tristate_ah_4b_2_q));  // open: dp
endmodule

module MIR (
  input  Clk,
  input  DEC_B0,
  input  DEC_B1,
  input  DEC_B2,
  input  DEC_A0,
  input  DEC_A1,
  input  DEC_A2,
  input  DEC_C0,
  input  DEC_C1,
  input  DEC_C2,
  input  BR,
  input  Wr,
  input  Rd,
  input  MBR,
  input  MAR,
  input  SH0,
  input  SH1,
  input  ALU0,
  input  ALU1,
  input  ALU2,
  input  AMUX,
  input  X0,
  input  X1,
  input  X2,
  input  X3,
  output Q0,
  output Q1,
  output Q2,
  output Q3,
  output Q4,
  output Q5,
  output Q6,
  output Q7,
  output Q8,
  output Q9,
  output Q10,
  output Q11,
  output Q12,
  output Q13,
  output Q14,
  output Q15,
  output Q16,
  output Q17,
  output Q18,
  output A19,
  output A20,
  output A21,
  output A22,
  output A23
);

  wire undriven;

  D_Flip_Flop d_ff_1 (.D(DEC_B0), .clk(Clk), .Q(Q0));  // open: Qn, preset, reset
  D_Flip_Flop d_ff_2 (.D(DEC_B1), .clk(Clk), .Q(Q1));  // open: Qn, preset, reset
  D_Flip_Flop d_ff_3 (.D(DEC_B2), .clk(Clk), .Q(Q2));  // open: Qn, preset, reset
  D_Flip_Flop d_ff_4 (.D(DEC_A0), .clk(Clk), .Q(Q3));  // open: Qn, preset, reset
  D_Flip_Flop d_ff_5 (.D(DEC_A1), .clk(Clk), .Q(Q4));  // open: Qn, preset, reset
  D_Flip_Flop d_ff_6 (.D(DEC_A2), .clk(Clk), .Q(Q5));  // open: Qn, preset, reset
  D_Flip_Flop d_ff_7 (.D(DEC_C0), .clk(Clk), .Q(Q6));  // open: Qn, preset, reset
  D_Flip_Flop d_ff_8 (.D(DEC_C1), .clk(Clk), .Q(Q7));  // open: Qn, preset, reset
  D_Flip_Flop d_ff_9 (.D(DEC_C2), .clk(Clk), .Q(Q8));  // open: Qn, preset, reset
  D_Flip_Flop d_ff_10 (.D(BR), .clk(Clk), .Q(Q9));  // open: Qn, preset, reset
  D_Flip_Flop d_ff_11 (.D(Wr), .clk(Clk), .Q(Q10));  // open: Qn, preset, reset
  D_Flip_Flop d_ff_12 (.D(Rd), .clk(Clk), .Q(Q11));  // open: Qn, preset, reset
  D_Flip_Flop d_ff_13 (.D(MBR), .clk(Clk), .Q(Q12));  // open: Qn, preset, reset
  D_Flip_Flop d_ff_14 (.D(MAR), .clk(Clk), .Q(Q13));  // open: Qn, preset, reset
  D_Flip_Flop d_ff_15 (.D(SH0), .clk(Clk), .Q(Q14));  // open: Qn, preset, reset
  D_Flip_Flop d_ff_16 (.D(SH1), .Q(Q15));  // open: clk, Qn, preset, reset
  D_Flip_Flop d_ff_17 (.D(ALU0), .clk(Clk), .Q(Q16));  // open: Qn, preset, reset
  D_Flip_Flop d_ff_18 (.D(ALU1), .clk(Clk), .Q(Q17));  // open: Qn, preset, reset
  D_Flip_Flop d_ff_19 (.D(ALU2), .clk(Clk), .Q(Q18));  // open: Qn, preset, reset
  D_Flip_Flop d_ff_20 (.D(AMUX), .clk(Clk), .Q(A19));  // open: Qn, preset, reset
  D_Flip_Flop d_ff_21 (.clk(undriven), .Q(A20));  // open: D, Qn, preset, reset
  D_Flip_Flop d_ff_22 (.clk(undriven), .Q(A21));  // open: D, Qn, preset, reset
  D_Flip_Flop d_ff_23 (.clk(undriven), .Q(A22));  // open: D, Qn, preset, reset
  D_Flip_Flop d_ff_24 (.clk(undriven), .Q(A23));  // open: D, Qn, preset, reset
endmodule

module MIR_Bank (
  input  E4,
  input  E3,
  input  E2,
  input  E1,
  input  E0,
  output Q0,
  output Q1,
  output Q2,
  output Q3,
  output Q4,
  output Q5,
  output Q6,
  output Q7,
  output Q8,
  output Q9,
  output Q10,
  output Q11,
  output Q12,
  output Q13,
  output Q14,
  output Q15,
  output Q16,
  output Q17,
  output Q18,
  output Q19,
  output Q20,
  output Q21,
  output Q22,
  output Q23
);

  Hex_Digit_Display Display_E1 (.value({3'b000, E4}));  // open: dp
  Hex_Digit_Display Display_E0 (.value({E3, E2, E1, E0}));  // open: dp
  ROM #(.addrWidth(5), .dataWidth(24)) ROM_32x24 (
    .addr({E4, E3, E2, E1, E0}),
    .data({Q23, Q22, Q21, Q20, Q19, Q18, Q17, Q16, Q15, Q14, Q13, Q12, Q11, Q10, Q9, Q8, Q7, Q6, Q5, Q4, Q3, Q2, Q1, Q0}));
  Hex_Digit_Display Display_Q5 (.value({Q23, Q22, Q21, Q20}));  // open: dp
  Hex_Digit_Display Display_Q4 (.value({Q19, Q18, Q17, Q16}));  // open: dp
  Hex_Digit_Display Display_Q3 (.value({Q15, Q14, Q13, Q12}));  // open: dp
  Hex_Digit_Display Display_Q2 (.value({Q11, Q10, Q9, Q8}));  // open: dp
  Hex_Digit_Display Display_Q1 (.value({Q7, Q6, Q5, Q4}));  // open: dp
  Hex_Digit_Display Display_Q0 (.value({Q3, Q2, Q1, Q0}));  // open: dp

  // Notes on the sheet:
  //   contents of ROM_32x24 (hex, n*v repeats v):
  //   80a01 90a01 a0a01 b0a01 c0a01 d0a01 e0a01 f0a01 80a01 81002 81003 81004 81005 81006 81007 200 80a40
  //   80a80 80ac0 80b00 80b40 80b80 80bc0 200 81200 1a80 1a40 1a40 80201 200 200 200
endmodule

module Incrementer (
  input  Clear,
  input  Clk,
  output [4:0] S
);

  Counter #(.max('h1f), .width(5)) counter_1 (.clr(Clear), .clk(Clk), .Q(S));  // open: load, up, count, D, carry
endmodule

module Program (
  input  [4:0] E,
  output [4:0] out_2
);

  ROM #(.addrWidth(5), .dataWidth(5)) rom_1 (.addr(E), .data(out_2));
endmodule
