// Logisim project T3_LFNM_ULA_padrao.circ as structural Verilog
module DEMO_ula_4b (
  input  A3,
  input  A2,
  input  A1,
  input  A0,
  input  B3,
  input  B2,
  input  B1,
  input  B0,
  input  Op1,
  input  Op0,
  output S3,
  output S2,
  output S1,
  output S0
);

  Hex_Digit_Display hex_digit_display_1 (.value({A3, A2, A1, A0}));  // open: dp
  Hex_Digit_Display hex_digit_display_2 (.value({B3, B2, B1, B0}));  // open: dp
  ula_4b ula_4b_1 (
    .A1(A1), .A0(A0), .B3(B3), .B2(B2), .B1(B1), .B0(B0), .A3(A3), .A2(A2), .Op1(Op1), .Op0(Op0), .S3(S3),
    .S2(S2), .S1(S1), .S0(S0));
  Hex_Digit_Display hex_digit_display_3 (.value({S3, S2, S1, S0}));  // open: dp

  // Notes on the sheet:
  //   00 : Adder ( + )
  //   01 : Buffer ( # )
  //   10 : Nand ( !& )
  //   11 : Subtractor ( - )
endmodule

module ula_4b (
  input  A3,
  input  A2,
  input  A1,
  input  A0,
  input  B3,
  input  B2,
  input  B1,
  input  B0,
  input  Op1,
  input  Op0,
  output S3,
  output S2,
  output S1,
  output S0
);

  wire adder_4b_1_s0, adder_4b_1_s1, adder_4b_1_s2, adder_4b_1_s3, buffer_4b_1_s0, buffer_4b_1_s1,
       buffer_4b_1_s2, buffer_4b_1_s3, nand_4b_1_s0, nand_4b_1_s1, nand_4b_1_s2, nand_4b_1_s3,
       subtractor_4b_1_s0, subtractor_4b_1_s1, subtractor_4b_1_s2, subtractor_4b_1_s3;

  Adder_4b adder_4b_1 (
    .A1(A1), .A0(A0), .B3(B3), .B2(B2), .B1(B1), .B0(B0), .A3(A3), .A2(A2), .S3(adder_4b_1_s3),
    .S2(adder_4b_1_s2), .S1(adder_4b_1_s1), .S0(adder_4b_1_s0));  // open: Ci, Co
  Buffer_4b buffer_4b_1 (
    .A1(A1), .A0(A0), .A3(A3), .A2(A2), .S3(buffer_4b_1_s3), .S2(buffer_4b_1_s2), .S1(buffer_4b_1_s1),
    .S0(buffer_4b_1_s0));
  Nand_4b nand_4b_1 (
    .A1(A1), .A0(A0), .B3(B3), .B2(B2), .B1(B1), .B0(B0), .A3(A3), .A2(A2), .S3(nand_4b_1_s3),
    .S2(nand_4b_1_s2), .S1(nand_4b_1_s1), .S0(nand_4b_1_s0));
  Subtractor_4b subtractor_4b_1 (
    .A1(A1), .A0(A0), .B3(B3), .B2(B2), .B1(B1), .B0(B0), .A3(A3), .A2(A2), .S3(subtractor_4b_1_s3),
    .S2(subtractor_4b_1_s2), .S1(subtractor_4b_1_s1), .S0(subtractor_4b_1_s0));  // open: Bo
  Multiplexador_4op_4b multiplexador_4op_4b_1 (
    .A1(adder_4b_1_s1), .A0(adder_4b_1_s0), .B3(buffer_4b_1_s3), .B2(buffer_4b_1_s2), .B1(buffer_4b_1_s1),
    .B0(buffer_4b_1_s0), .C3(nand_4b_1_s3), .C2(nand_4b_1_s2), .A3(adder_4b_1_s3), .C1(nand_4b_1_s1),
    .C0(nand_4b_1_s0), .D3(subtractor_4b_1_s3), .D2(subtractor_4b_1_s2), .D1(subtractor_4b_1_s1),
    .D0(subtractor_4b_1_s0), .Op1(Op1), .Op0(Op0), .A2(adder_4b_1_s2), .S2(S2), .S1(S1), .S0(S0), .S3(S3));
endmodule

module Adder_Half (
  input  A,
  input  B,
  output S_Adh,
  output Co_Adh
);

  and and_1 (Co_Adh, A, B);
  xor xor_1 (S_Adh, A, B);

  // Notes on the sheet:
  //   S_Adh = A ⊕ B
  //   Co_Adh = A . B
endmodule

module Adder_1b (
  input  A,
  input  B,
  input  Ci,
  output S_Ad1b,
  output Co_Ad1b
);

  wire adder_half_1_co_adh, adder_half_1_s_adh, adder_half_2_co_adh;

  Adder_Half adder_half_1 (.A(A), .B(B), .S_Adh(adder_half_1_s_adh), .Co_Adh(adder_half_1_co_adh));
  Adder_Half adder_half_2 (.A(adder_half_1_s_adh), .B(Ci), .S_Adh(S_Ad1b), .Co_Adh(adder_half_2_co_adh));
  or or_1 (Co_Ad1b, adder_half_2_co_adh, adder_half_1_co_adh);

  // Notes on the sheet:
  //   S_Ad1b = A ⊕ B ⊕ Ci
  //   Co_Ad1b ​= (A.B) + ( Ci . (A⊕B) )
  //   T1 = A ⊕ B
  //   T2 = A.B
  //   T3 = Ci . T1
  //   S_Ad1b = T1 ⊕ Ci
  //   Co_Ad1b ​= T2 + T3
endmodule

module Adder_4b (
  input  A3,
  input  A2,
  input  A1,
  input  A0,
  input  B3,
  input  B2,
  input  B1,
  input  B0,
  input  Ci,
  output Co,
  output S3,
  output S2,
  output S1,
  output S0
);

  wire adder_1b_1_co_ad1b, adder_1b_2_co_ad1b, adder_1b_3_co_ad1b;

  Adder_1b adder_1b_1 (.A(A0), .B(B0), .Ci(Ci), .S_Ad1b(S0), .Co_Ad1b(adder_1b_1_co_ad1b));
  Adder_1b adder_1b_2 (.A(A1), .B(B1), .Ci(adder_1b_1_co_ad1b), .S_Ad1b(S1), .Co_Ad1b(adder_1b_2_co_ad1b));
  Adder_1b adder_1b_3 (.A(A2), .B(B2), .Ci(adder_1b_2_co_ad1b), .S_Ad1b(S2), .Co_Ad1b(adder_1b_3_co_ad1b));
  Adder_1b adder_1b_4 (.A(A3), .B(B3), .Ci(adder_1b_3_co_ad1b), .S_Ad1b(S3), .Co_Ad1b(Co));

  // Notes on the sheet:
  //   metodo:
  //   ripple-carry
endmodule

module Buffer_4b (
  input  A3,
  input  A2,
  input  A1,
  input  A0,
  output S3,
  output S2,
  output S1,
  output S0
);

  buf buffer_1 (S0, A0);
  buf buffer_2 (S1, A1);
  buf buffer_3 (S2, A2);
  buf buffer_4 (S3, A3);
endmodule

module Nand_4b (
  input  A3,
  input  A2,
  input  A1,
  input  A0,
  input  B3,
  input  B2,
  input  B1,
  input  B0,
  output S3,
  output S2,
  output S1,
  output S0
);

  nand nand_1 (S0, A0, B0);
  nand nand_2 (S1, A1, B1);
  nand nand_3 (S2, A2, B2);
  nand nand_4 (S3, A3, B3);
endmodule

module Subtractor_4b (
  input  A3,
  input  A2,
  input  A1,
  input  A0,
  input  B3,
  input  B2,
  input  B1,
  input  B0,
  output S3,
  output S2,
  output S1,
  output S0,
  output Bo
);

  wire nand_4b_1_s0, nand_4b_1_s1, nand_4b_1_s2, nand_4b_1_s3;

  Nand_4b nand_4b_1 (
    .A1(B1), .A0(B0), .B3(B3), .B2(B2), .B1(B1), .B0(B0), .A3(B3), .A2(B2), .S3(nand_4b_1_s3),
    .S2(nand_4b_1_s2), .S1(nand_4b_1_s1), .S0(nand_4b_1_s0));
  Adder_4b adder_4b_1 (
    .A1(A1), .A0(A0), .B3(nand_4b_1_s3), .B2(nand_4b_1_s2), .B1(nand_4b_1_s1), .B0(nand_4b_1_s0), .Ci(1'b1),
    .A3(A3), .A2(A2), .Co(Bo), .S3(S3), .S2(S2), .S1(S1), .S0(S0));
endmodule

module Decoder_4op_1b (
  input  o0,
  input  o1,
  output m0,
  output m1,
  output m2,
  output m3
);

  wire buffer_1_out, buffer_2_out, not_1_out, not_2_out;

  buf buffer_1 (buffer_1_out, o1);
  buf buffer_2 (buffer_2_out, o0);
  not not_1 (not_1_out, o1);
  not not_2 (not_2_out, o0);
  and and_1 (m0, not_2_out, not_1_out);
  and and_2 (m1, not_1_out, buffer_2_out);
  and and_3 (m2, not_2_out, buffer_1_out);
  and and_4 (m3, buffer_2_out, buffer_1_out);
endmodule

module Multiplexador_4op_1b (
  input  i0,
  input  i1,
  input  i2,
  input  i3,
  input  Op0,
  input  Op1,
  output S
);

  wire and_1_out, and_2_out, and_3_out, and_4_out, decoder_4op_1b_1_m0, decoder_4op_1b_1_m1,
       decoder_4op_1b_1_m2, decoder_4op_1b_1_m3;

  Decoder_4op_1b decoder_4op_1b_1 (
    .o0(Op0), .o1(Op1), .m0(decoder_4op_1b_1_m0), .m1(decoder_4op_1b_1_m1), .m2(decoder_4op_1b_1_m2),
    .m3(decoder_4op_1b_1_m3));
  and and_1 (and_1_out, decoder_4op_1b_1_m3, i3);
  and and_2 (and_2_out, decoder_4op_1b_1_m2, i2);
  and and_3 (and_3_out, decoder_4op_1b_1_m1, i1);
  and and_4 (and_4_out, decoder_4op_1b_1_m0, i0);
  or or_1 (S, and_1_out, and_2_out, and_3_out, and_4_out);
endmodule

module Multiplexador_4op_4b (
  input  A3,
  input  A2,
  input  A1,
  input  A0,
  input  B3,
  input  B2,
  input  B1,
  input  B0,
  input  C3,
  input  C2,
  input  C1,
  input  C0,
  input  D3,
  input  D2,
  input  D1,
  input  D0,
  input  Op1,
  input  Op0,
  output S3,
  output S2,
  output S1,
  output S0
);

  Multiplexador_4op_1b multiplexador_4op_1b_1 (.i3(D0), .i0(A0), .i1(B0), .i2(C0), .Op0(Op0), .Op1(Op1), .S(S0));
  Multiplexador_4op_1b multiplexador_4op_1b_2 (.i3(D1), .i0(A1), .i1(B1), .i2(C1), .Op0(Op0), .Op1(Op1), .S(S1));
  Multiplexador_4op_1b multiplexador_4op_1b_3 (.i3(D2), .i0(A2), .i1(B2), .i2(C2), .Op0(Op0), .Op1(Op1), .S(S2));
  Multiplexador_4op_1b multiplexador_4op_1b_4 (.i3(D3), .i0(A3), .i1(B3), .i2(C3), .Op0(Op0), .Op1(Op1), .S(S3));
endmodule
